// Logisim project da1_task1.circ as structural Verilog: 4 circuits, main circuit DUT
module DUT (
  input  [6:0] A,
  output [31:0] X3,
  output [31:0] X2,
  output [31:0] X1,
  output [31:0] X0
);

  wire bitselector_1_out, bitselector_2_out, not_1_out, not_2_out;
  wire [4:0] bitselector_3_out;
  wire [31:0] bit_extender_1_out, bit_extender_2_out, bit_extender_3_out, bit_extender_4_out,
       m_decd_1_out_7ea727ee;

  BitSelector #(.width(7)) bitselector_1 (.in(A), .out(bitselector_1_out), .sel(3'b110));
  BitSelector #(.width(7)) bitselector_2 (.in(A), .out(bitselector_2_out), .sel(3'b101));
  BitSelector #(.width(7), .group(5)) bitselector_3 (.in(A), .out(bitselector_3_out), .sel(1'b0));
  not not_1 (not_1_out, bitselector_1_out);
  not not_2 (not_2_out, bitselector_2_out);
  m_decd m_decd_1 (.in_10ffbee2(bitselector_3_out), .out_7ea727ee(m_decd_1_out_7ea727ee));
  assign bit_extender_1_out = {{31{bitselector_1_out}}, bitselector_1_out};  // Bit_Extender bit_extender_1
  assign bit_extender_2_out = {{31{not_1_out}}, not_1_out};  // Bit_Extender bit_extender_2
  assign bit_extender_3_out = {{31{bitselector_2_out}}, bitselector_2_out};  // Bit_Extender bit_extender_3
  assign bit_extender_4_out = {{31{not_2_out}}, not_2_out};  // Bit_Extender bit_extender_4
  assign X3 = bit_extender_1_out & bit_extender_3_out & m_decd_1_out_7ea727ee;  // AND_Gate and_1, 32 bits wide
  assign X2 = bit_extender_1_out & bit_extender_4_out & m_decd_1_out_7ea727ee;  // AND_Gate and_2, 32 bits wide
  assign X1 = bit_extender_2_out & bit_extender_3_out & m_decd_1_out_7ea727ee;  // AND_Gate and_3, 32 bits wide
  assign X0 = bit_extender_2_out & bit_extender_4_out & m_decd_1_out_7ea727ee;  // AND_Gate and_4, 32 bits wide

  // Notes on the sheet:
  //   Please put your deisgn below. You may also use subcircuits.
  //   However, do not move or rename any pins.
  //   The input pins are in binary, the output in hex.
endmodule

module TB (
  input  [6:0] A,
  output [31:0] X3,
  output [31:0] X2,
  output [31:0] X1,
  output [31:0] X0
);

  DUT dut_1 (.A(A), .X3(X3), .X2(X2), .X1(X1), .X0(X0));

  // Notes on the sheet:
  //   DO NOT MODIFY THIS
  //   TEST YOUR CIRCUITS USING THIS TO MAKE SURE YOU HAVE NOT ALTERED PIN OUT
endmodule

module ind_vec (
  input  in0,
  input  in1,
  input  in2,
  input  in3,
  input  in4,
  input  in5,
  input  in6,
  input  in7,
  input  in8,
  input  in9,
  input  in10,
  input  in11,
  input  in12,
  input  in13,
  input  in14,
  input  in15,
  input  in16,
  input  in17,
  input  in18,
  input  in19,
  input  in20,
  input  in21,
  input  in22,
  input  in23,
  input  in24,
  input  in25,
  input  in26,
  input  in27,
  input  in28,
  input  in29,
  input  in30,
  input  in31,
  output [31:0] out_7ea727ee
);

  wire [31:0] adder_1_out, adder_2_out, adder_3_out, adder_4_out, adder_5_out, adder_6_out, adder_7_out,
       adder_8_out, adder_9_out, adder_10_out, adder_11_out, adder_12_out, adder_13_out, adder_14_out,
       adder_15_out, adder_16_out, adder_17_out, adder_18_out, adder_19_out, adder_20_out, adder_21_out,
       adder_22_out, adder_23_out, adder_24_out, adder_25_out, adder_26_out, adder_27_out, adder_28_out,
       adder_29_out, adder_30_out, bit_extender_1_out, bit_extender_2_out, bit_extender_3_out,
       bit_extender_4_out, bit_extender_5_out, bit_extender_6_out, bit_extender_7_out, bit_extender_8_out,
       bit_extender_9_out, bit_extender_10_out, bit_extender_11_out, bit_extender_12_out,
       bit_extender_13_out, bit_extender_14_out, bit_extender_15_out, bit_extender_16_out,
       bit_extender_17_out, bit_extender_18_out, bit_extender_19_out, bit_extender_20_out,
       bit_extender_21_out, bit_extender_22_out, bit_extender_23_out, bit_extender_24_out,
       bit_extender_25_out, bit_extender_26_out, bit_extender_27_out, bit_extender_28_out,
       bit_extender_29_out, bit_extender_30_out, bit_extender_31_out, bit_extender_32_out, shifter_1_out,
       shifter_2_out, shifter_3_out, shifter_4_out, shifter_5_out, shifter_6_out, shifter_7_out,
       shifter_8_out, shifter_9_out, shifter_10_out, shifter_11_out, shifter_12_out, shifter_13_out,
       shifter_14_out, shifter_15_out, shifter_16_out, shifter_17_out, shifter_18_out, shifter_19_out,
       shifter_20_out, shifter_21_out, shifter_22_out, shifter_23_out, shifter_24_out, shifter_25_out,
       shifter_26_out, shifter_27_out, shifter_28_out, shifter_29_out, shifter_30_out, shifter_31_out;

  // Probe on bit_extender_2_out
  assign bit_extender_1_out = {{31{1'b0}}, in0};  // Bit_Extender bit_extender_1
  assign bit_extender_2_out = {{31{1'b0}}, in1};  // Bit_Extender bit_extender_2
  assign bit_extender_3_out = {{31{1'b0}}, in2};  // Bit_Extender bit_extender_3
  assign bit_extender_4_out = {{31{1'b0}}, in3};  // Bit_Extender bit_extender_4
  assign bit_extender_5_out = {{31{1'b0}}, in4};  // Bit_Extender bit_extender_5
  assign bit_extender_6_out = {{31{1'b0}}, in5};  // Bit_Extender bit_extender_6
  assign bit_extender_7_out = {{31{1'b0}}, in6};  // Bit_Extender bit_extender_7
  assign bit_extender_8_out = {{31{1'b0}}, in7};  // Bit_Extender bit_extender_8
  assign bit_extender_9_out = {{31{1'b0}}, in8};  // Bit_Extender bit_extender_9
  assign bit_extender_10_out = {{31{1'b0}}, in9};  // Bit_Extender bit_extender_10
  assign bit_extender_11_out = {{31{1'b0}}, in10};  // Bit_Extender bit_extender_11
  assign bit_extender_12_out = {{31{1'b0}}, in11};  // Bit_Extender bit_extender_12
  assign bit_extender_13_out = {{31{1'b0}}, in12};  // Bit_Extender bit_extender_13
  assign bit_extender_14_out = {{31{1'b0}}, in13};  // Bit_Extender bit_extender_14
  assign bit_extender_15_out = {{31{1'b0}}, in14};  // Bit_Extender bit_extender_15
  assign bit_extender_16_out = {{31{1'b0}}, in15};  // Bit_Extender bit_extender_16
  assign bit_extender_17_out = {{31{1'b0}}, in16};  // Bit_Extender bit_extender_17
  assign bit_extender_18_out = {{31{1'b0}}, in17};  // Bit_Extender bit_extender_18
  assign bit_extender_19_out = {{31{1'b0}}, in18};  // Bit_Extender bit_extender_19
  assign bit_extender_20_out = {{31{1'b0}}, in19};  // Bit_Extender bit_extender_20
  assign bit_extender_21_out = {{31{1'b0}}, in20};  // Bit_Extender bit_extender_21
  assign bit_extender_22_out = {{31{1'b0}}, in21};  // Bit_Extender bit_extender_22
  assign bit_extender_23_out = {{31{1'b0}}, in22};  // Bit_Extender bit_extender_23
  assign bit_extender_24_out = {{31{1'b0}}, in23};  // Bit_Extender bit_extender_24
  assign bit_extender_25_out = {{31{1'b0}}, in24};  // Bit_Extender bit_extender_25
  assign bit_extender_26_out = {{31{1'b0}}, in25};  // Bit_Extender bit_extender_26
  assign bit_extender_27_out = {{31{1'b0}}, in26};  // Bit_Extender bit_extender_27
  assign bit_extender_28_out = {{31{1'b0}}, in27};  // Bit_Extender bit_extender_28
  assign bit_extender_29_out = {{31{1'b0}}, in28};  // Bit_Extender bit_extender_29
  assign bit_extender_30_out = {{31{1'b0}}, in29};  // Bit_Extender bit_extender_30
  assign bit_extender_31_out = {{31{1'b0}}, in30};  // Bit_Extender bit_extender_31
  assign bit_extender_32_out = {{31{1'b0}}, in31};  // Bit_Extender bit_extender_32
  // Probe on bit_extender_1_out
  Shifter #(.width(32)) shifter_1 (.in(bit_extender_2_out), .\dist (5'b00001), .out(shifter_1_out));
  Shifter #(.width(32)) shifter_2 (.in(bit_extender_3_out), .\dist (5'b00010), .out(shifter_2_out));
  Shifter #(.width(32)) shifter_3 (.in(bit_extender_4_out), .\dist (5'b00011), .out(shifter_3_out));
  Shifter #(.width(32)) shifter_4 (.in(bit_extender_5_out), .\dist (5'b00100), .out(shifter_4_out));
  Shifter #(.width(32)) shifter_5 (.in(bit_extender_6_out), .\dist (5'b00101), .out(shifter_5_out));
  Shifter #(.width(32)) shifter_6 (.in(bit_extender_7_out), .\dist (5'b00110), .out(shifter_6_out));
  Shifter #(.width(32)) shifter_7 (.in(bit_extender_8_out), .\dist (5'b00111), .out(shifter_7_out));
  Shifter #(.width(32)) shifter_8 (.in(bit_extender_9_out), .\dist (5'b01000), .out(shifter_8_out));
  Shifter #(.width(32)) shifter_9 (.in(bit_extender_10_out), .\dist (5'b01001), .out(shifter_9_out));
  Shifter #(.width(32)) shifter_10 (.in(bit_extender_11_out), .\dist (5'b01010), .out(shifter_10_out));
  Shifter #(.width(32)) shifter_11 (.in(bit_extender_12_out), .\dist (5'b01011), .out(shifter_11_out));
  Shifter #(.width(32)) shifter_12 (.in(bit_extender_13_out), .\dist (5'b01100), .out(shifter_12_out));
  Shifter #(.width(32)) shifter_13 (.in(bit_extender_14_out), .\dist (5'b01101), .out(shifter_13_out));
  Shifter #(.width(32)) shifter_14 (.in(bit_extender_15_out), .\dist (5'b01110), .out(shifter_14_out));
  Shifter #(.width(32)) shifter_15 (.in(bit_extender_16_out), .\dist (5'b01111), .out(shifter_15_out));
  Shifter #(.width(32)) shifter_16 (.in(bit_extender_17_out), .\dist (5'b10000), .out(shifter_16_out));
  Shifter #(.width(32)) shifter_17 (.in(bit_extender_18_out), .\dist (5'b10001), .out(shifter_17_out));
  Shifter #(.width(32)) shifter_18 (.in(bit_extender_19_out), .\dist (5'b10010), .out(shifter_18_out));
  Shifter #(.width(32)) shifter_19 (.in(bit_extender_20_out), .\dist (5'b10011), .out(shifter_19_out));
  Shifter #(.width(32)) shifter_20 (.in(bit_extender_21_out), .\dist (5'b10100), .out(shifter_20_out));
  Shifter #(.width(32)) shifter_21 (.in(bit_extender_22_out), .\dist (5'b10101), .out(shifter_21_out));
  Shifter #(.width(32)) shifter_22 (.in(bit_extender_23_out), .\dist (5'b10110), .out(shifter_22_out));
  Shifter #(.width(32)) shifter_23 (.in(bit_extender_24_out), .\dist (5'b10111), .out(shifter_23_out));
  Shifter #(.width(32)) shifter_24 (.in(bit_extender_25_out), .\dist (5'b11000), .out(shifter_24_out));
  Shifter #(.width(32)) shifter_25 (.in(bit_extender_26_out), .\dist (5'b11001), .out(shifter_25_out));
  Shifter #(.width(32)) shifter_26 (.in(bit_extender_27_out), .\dist (5'b11010), .out(shifter_26_out));
  Shifter #(.width(32)) shifter_27 (.in(bit_extender_28_out), .\dist (5'b11011), .out(shifter_27_out));
  Shifter #(.width(32)) shifter_28 (.in(bit_extender_29_out), .\dist (5'b11100), .out(shifter_28_out));
  Shifter #(.width(32)) shifter_29 (.in(bit_extender_30_out), .\dist (5'b11101), .out(shifter_29_out));
  Shifter #(.width(32)) shifter_30 (.in(bit_extender_31_out), .\dist (5'b11110), .out(shifter_30_out));
  Shifter #(.width(32)) shifter_31 (.in(bit_extender_32_out), .\dist ({5{1'b1}}), .out(shifter_31_out));
  // Probe on shifter_1_out
  Adder #(.width(32)) adder_1 (.a(bit_extender_1_out), .b(shifter_1_out), .out(adder_1_out));  // open: cin, cout
  Adder #(.width(32)) adder_2 (.a(shifter_2_out), .b(shifter_3_out), .out(adder_2_out));  // open: cin, cout
  Adder #(.width(32)) adder_3 (.a(shifter_4_out), .b(shifter_5_out), .out(adder_3_out));  // open: cin, cout
  Adder #(.width(32)) adder_4 (.a(shifter_6_out), .b(shifter_7_out), .out(adder_4_out));  // open: cin, cout
  Adder #(.width(32)) adder_5 (.a(shifter_8_out), .b(shifter_9_out), .out(adder_5_out));  // open: cin, cout
  Adder #(.width(32)) adder_6 (.a(shifter_10_out), .b(shifter_11_out), .out(adder_6_out));  // open: cin, cout
  Adder #(.width(32)) adder_7 (.a(shifter_12_out), .b(shifter_13_out), .out(adder_7_out));  // open: cin, cout
  Adder #(.width(32)) adder_8 (.a(shifter_14_out), .b(shifter_15_out), .out(adder_8_out));  // open: cin, cout
  Adder #(.width(32)) adder_9 (.a(shifter_16_out), .b(shifter_17_out), .out(adder_9_out));  // open: cin, cout
  Adder #(.width(32)) adder_10 (.a(shifter_18_out), .b(shifter_19_out), .out(adder_10_out));  // open: cin, cout
  Adder #(.width(32)) adder_11 (.a(shifter_20_out), .b(shifter_21_out), .out(adder_11_out));  // open: cin, cout
  Adder #(.width(32)) adder_12 (.a(shifter_22_out), .b(shifter_23_out), .out(adder_12_out));  // open: cin, cout
  Adder #(.width(32)) adder_13 (.a(shifter_24_out), .b(shifter_25_out), .out(adder_13_out));  // open: cin, cout
  Adder #(.width(32)) adder_14 (.a(shifter_26_out), .b(shifter_27_out), .out(adder_14_out));  // open: cin, cout
  Adder #(.width(32)) adder_15 (.a(shifter_28_out), .b(shifter_29_out), .out(adder_15_out));  // open: cin, cout
  Adder #(.width(32)) adder_16 (.a(shifter_30_out), .b(shifter_31_out), .out(adder_16_out));  // open: cin, cout
  Adder #(.width(32)) adder_17 (.a(adder_1_out), .b(adder_2_out), .out(adder_17_out));  // open: cin, cout
  Adder #(.width(32)) adder_18 (.a(adder_3_out), .b(adder_4_out), .out(adder_18_out));  // open: cin, cout
  Adder #(.width(32)) adder_19 (.a(adder_5_out), .b(adder_6_out), .out(adder_19_out));  // open: cin, cout
  Adder #(.width(32)) adder_20 (.a(adder_7_out), .b(adder_8_out), .out(adder_20_out));  // open: cin, cout
  Adder #(.width(32)) adder_21 (.a(adder_9_out), .b(adder_10_out), .out(adder_21_out));  // open: cin, cout
  Adder #(.width(32)) adder_22 (.a(adder_11_out), .b(adder_12_out), .out(adder_22_out));  // open: cin, cout
  Adder #(.width(32)) adder_23 (.a(adder_13_out), .b(adder_14_out), .out(adder_23_out));  // open: cin, cout
  Adder #(.width(32)) adder_24 (.a(adder_15_out), .b(adder_16_out), .out(adder_24_out));  // open: cin, cout
  Adder #(.width(32)) adder_25 (.a(adder_17_out), .b(adder_18_out), .out(adder_25_out));  // open: cin, cout
  Adder #(.width(32)) adder_26 (.a(adder_19_out), .b(adder_20_out), .out(adder_26_out));  // open: cin, cout
  Adder #(.width(32)) adder_27 (.a(adder_21_out), .b(adder_22_out), .out(adder_27_out));  // open: cin, cout
  Adder #(.width(32)) adder_28 (.a(adder_23_out), .b(adder_24_out), .out(adder_28_out));  // open: cin, cout
  Adder #(.width(32)) adder_29 (.a(adder_25_out), .b(adder_26_out), .out(adder_29_out));  // open: cin, cout
  Adder #(.width(32)) adder_30 (.a(adder_27_out), .b(adder_28_out), .out(adder_30_out));  // open: cin, cout
  Adder #(.width(32)) adder_31 (.a(adder_29_out), .b(adder_30_out), .out(out_7ea727ee));  // open: cin, cout
endmodule

module m_decd (
  input  [4:0] in_10ffbee2,
  output [31:0] out_7ea727ee
);

  wire decoder_1_out0, decoder_1_out1, decoder_1_out2, decoder_1_out3, decoder_1_out4, decoder_1_out5,
       decoder_1_out6, decoder_1_out7, decoder_1_out8, decoder_1_out9, decoder_1_out10, decoder_1_out11,
       decoder_1_out12, decoder_1_out13, decoder_1_out14, decoder_1_out15, decoder_1_out16, decoder_1_out17,
       decoder_1_out18, decoder_1_out19, decoder_1_out20, decoder_1_out21, decoder_1_out22, decoder_1_out23,
       decoder_1_out24, decoder_1_out25, decoder_1_out26, decoder_1_out27, decoder_1_out28, decoder_1_out29,
       decoder_1_out30, decoder_1_out31;

  Decoder #(.select(5), .enable("false")) decoder_1 (
    .out0(decoder_1_out0), .out1(decoder_1_out1), .out2(decoder_1_out2), .out3(decoder_1_out3),
    .out4(decoder_1_out4), .out5(decoder_1_out5), .out6(decoder_1_out6), .out7(decoder_1_out7),
    .out8(decoder_1_out8), .out9(decoder_1_out9), .out10(decoder_1_out10), .out11(decoder_1_out11),
    .out12(decoder_1_out12), .out13(decoder_1_out13), .out14(decoder_1_out14), .out15(decoder_1_out15),
    .out16(decoder_1_out16), .out17(decoder_1_out17), .out18(decoder_1_out18), .out19(decoder_1_out19),
    .out20(decoder_1_out20), .out21(decoder_1_out21), .out22(decoder_1_out22), .out23(decoder_1_out23),
    .out24(decoder_1_out24), .out25(decoder_1_out25), .out26(decoder_1_out26), .out27(decoder_1_out27),
    .out28(decoder_1_out28), .out29(decoder_1_out29), .out30(decoder_1_out30), .out31(decoder_1_out31),
    .sel(in_10ffbee2));
  // Probe on decoder_1_out0
  // Probe on decoder_1_out1
  // Probe on decoder_1_out4
  ind_vec ind_vec_1 (
    .in22(decoder_1_out22), .in20(decoder_1_out20), .in18(decoder_1_out18), .in16(decoder_1_out16),
    .in14(decoder_1_out14), .in12(decoder_1_out12), .in10(decoder_1_out10), .in8(decoder_1_out8),
    .in6(decoder_1_out6), .in4(decoder_1_out4), .in2(decoder_1_out2), .in0(decoder_1_out0),
    .in1(decoder_1_out1), .in3(decoder_1_out3), .in5(decoder_1_out5), .in7(decoder_1_out7),
    .in9(decoder_1_out9), .in11(decoder_1_out11), .in13(decoder_1_out13), .in15(decoder_1_out15),
    .in17(decoder_1_out17), .in19(decoder_1_out19), .in21(decoder_1_out21), .in23(decoder_1_out23),
    .in24(decoder_1_out24), .in25(decoder_1_out25), .in26(decoder_1_out26), .in27(decoder_1_out27),
    .in28(decoder_1_out28), .in29(decoder_1_out29), .in30(decoder_1_out30), .in31(decoder_1_out31),
    .out_7ea727ee(out_7ea727ee));
endmodule
