// Logisim project da1_task2.circ as structural Verilog: 6 circuits, main circuit DUT
module DUT (
  input  [3:0] A,
  input  [3:0] B,
  input  [3:0] C,
  output [3:0] MEDIAN
);

  med med_1 (.A(A), .B(B), .C(C), .MEDIAN_(MEDIAN));

  // Notes on the sheet:
  //   Please put your deisgn below. You may also use subcircuits.
  //   However, do not move or rename any pins.
endmodule

module TB (
  input  [3:0] A,
  input  [3:0] B,
  input  [3:0] C,
  output [3:0] MEDIAN
);

  DUT dut_1 (.A(A), .B(B), .C(C), .MEDIAN(MEDIAN));

  // Notes on the sheet:
  //   DO NOT MODIFY THIS
  //   TEST YOUR CIRCUITS USING THIS TO MAKE SURE YOU HAVE NOT ALTERED PIN OUT
endmodule

module le (
  input  [3:0] in0,
  input  [3:0] in1,
  output [3:0] out_
);

  wire comparator_1_eq, comparator_1_lt, or_1_out;

  Comparator #(.width(4), .mode("unsigned")) comparator_1 (
    .a(in0), .b(in1), .eq(comparator_1_eq), .lt(comparator_1_lt));  // open: gt
  // Probe on comparator_1_lt
  // Probe on comparator_1_eq
  or or_1 (or_1_out, comparator_1_eq, comparator_1_lt);
  assign out_ = {{3{or_1_out}}, or_1_out};  // Bit_Extender bit_extender_1
endmodule

module median (
  input  [3:0] A,
  input  [3:0] B,
  input  [3:0] C,
  output [3:0] MEDIAN
);

  wire [3:0] AleB_out_, and_1_out, and_2_out, and_3_out, BleC_out_, CleA_out_, s12_out, s13_out, s23_out;

  // Probe on AleB_out_
  le AleB (.in0(A), .in1(B), .out_(AleB_out_));
  le BleC (.in0(B), .in1(C), .out_(BleC_out_));
  le CleA (.in0(C), .in1(A), .out_(CleA_out_));
  assign s12_out = AleB_out_ & BleC_out_;  // AND_Gate s12, 4 bits wide
  assign s23_out = BleC_out_ & CleA_out_;  // AND_Gate s23, 4 bits wide
  assign s13_out = CleA_out_ & AleB_out_;  // AND_Gate s13, 4 bits wide
  assign and_1_out = B & s12_out;  // AND_Gate and_1, 4 bits wide
  // Probe on and_2_out
  assign and_2_out = C & s23_out;  // AND_Gate and_2, 4 bits wide
  assign and_3_out = s13_out & A;  // AND_Gate and_3, 4 bits wide
  // Probe on and_1_out
  // Probe on and_3_out
  assign MEDIAN = and_1_out | and_2_out | and_3_out;  // OR_Gate or_1, 4 bits wide
endmodule

module ascend (
  input  [3:0] min,
  input  [3:0] med,
  input  [3:0] max,
  output [3:0] ascending
);

  wire [3:0] le_1_out_, le_2_out_;

  // Probe on med
  le le_1 (.in0(min), .in1(med), .out_(le_1_out_));
  le le_2 (.in0(med), .in1(max), .out_(le_2_out_));
  // Probe on le_1_out_
  // Probe on le_2_out_
  assign ascending = le_1_out_ & le_2_out_;  // AND_Gate and_1, 4 bits wide
endmodule

module med (
  input  [3:0] A,
  input  [3:0] B,
  input  [3:0] C,
  output [3:0] MEDIAN_
);

  wire [3:0] and_1_out, and_2_out, and_3_out, ascend_1_ascending, ascend_2_ascending, ascend_3_ascending,
       ascend_4_ascending, ascend_5_ascending, ascend_6_ascending, or_1_out, or_2_out, or_3_out;

  ascend ascend_1 (.min(B), .med(A), .max(C), .ascending(ascend_1_ascending));
  ascend ascend_2 (.min(C), .med(A), .max(B), .ascending(ascend_2_ascending));
  ascend ascend_3 (.min(A), .med(B), .max(C), .ascending(ascend_3_ascending));
  ascend ascend_4 (.min(C), .med(B), .max(A), .ascending(ascend_4_ascending));
  ascend ascend_5 (.min(A), .med(C), .max(B), .ascending(ascend_5_ascending));
  ascend ascend_6 (.min(B), .med(C), .max(A), .ascending(ascend_6_ascending));
  assign or_1_out = ascend_1_ascending | ascend_2_ascending;  // OR_Gate or_1, 4 bits wide
  assign or_2_out = ascend_3_ascending | ascend_4_ascending;  // OR_Gate or_2, 4 bits wide
  // Probe on or_2_out
  // Probe on or_3_out
  assign or_3_out = ascend_5_ascending | ascend_6_ascending;  // OR_Gate or_3, 4 bits wide
  // Probe on or_1_out
  assign and_1_out = A & or_1_out;  // AND_Gate and_1, 4 bits wide
  assign and_2_out = B & or_2_out;  // AND_Gate and_2, 4 bits wide
  assign and_3_out = or_3_out & C;  // AND_Gate and_3, 4 bits wide
  assign MEDIAN_ = and_1_out | and_2_out | and_3_out;  // OR_Gate or_4, 4 bits wide

  // Notes on the sheet:
  //   BAC
  //   CAB
  //   ABC
  //   CBA
  //   ACB
  //   BCA
endmodule
