// Logisim project da1_task3.circ as structural Verilog: 5 circuits, main circuit DUT
module DUT (
  input  [5:0] CODON,
  output [4:0] AA
);

  splitBits splitbits_1 (.CODON(CODON), .out_2(AA));

  // Notes on the sheet:
  //   Please put your deisgn below. You may also use subcircuits.
  //   However, do not move or rename any pins.
endmodule

module TB (
  input  [5:0] CODON,
  output [4:0] AA
);

  DUT dut_1 (.CODON(CODON), .AA(AA));

  // Notes on the sheet:
  //   DO NOT MODIFY THIS
  //   TEST YOUR CIRCUITS USING THIS TO MAKE SURE YOU HAVE NOT ALTERED PIN OUT
endmodule

module splitBits (
  input  [5:0] CODON,
  output [4:0] out_2
);

  wire bitselector_1_out, bitselector_2_out, bitselector_3_out, bitselector_4_out, bitselector_5_out,
       bitselector_6_out, c2a_splitted_1_a0, c2a_splitted_1_a1, c2a_splitted_1_a2, c2a_splitted_1_a3,
       c2a_splitted_1_a4;

  BitSelector #(.width(6)) bitselector_1 (.in(CODON), .out(bitselector_1_out), .sel(3'b101));
  BitSelector #(.width(6)) bitselector_2 (.in(CODON), .out(bitselector_2_out), .sel(3'b100));
  BitSelector #(.width(6)) bitselector_3 (.in(CODON), .out(bitselector_3_out), .sel(3'b011));
  BitSelector #(.width(6)) bitselector_4 (.in(CODON), .out(bitselector_4_out), .sel(3'b010));
  BitSelector #(.width(6)) bitselector_5 (.in(CODON), .out(bitselector_5_out), .sel(3'b001));
  BitSelector #(.width(6)) bitselector_6 (.in(CODON), .out(bitselector_6_out), .sel(3'b000));
  C2A_splitted c2a_splitted_1 (
    .c5(bitselector_1_out), .c4(bitselector_2_out), .c3(bitselector_3_out), .c2(bitselector_4_out),
    .c1(bitselector_5_out), .c0(bitselector_6_out), .a4(c2a_splitted_1_a4), .a3(c2a_splitted_1_a3),
    .a2(c2a_splitted_1_a2), .a1(c2a_splitted_1_a1), .a0(c2a_splitted_1_a0));
  concat concat_1 (
    .a0(c2a_splitted_1_a0), .a1(c2a_splitted_1_a1), .a2(c2a_splitted_1_a2), .a3(c2a_splitted_1_a3),
    .a4(c2a_splitted_1_a4), .aa(out_2));
endmodule

module C2A_splitted (
  input  c5,
  input  c4,
  input  c3,
  input  c2,
  input  c1,
  input  c0,
  output a4,
  output a3,
  output a2,
  output a1,
  output a0
);

  wire and_2_out, and_3_out, and_4_out, and_5_out, and_6_out, and_7_out, and_8_out, and_9_out, and_10_out,
       and_11_out, and_12_out, and_13_out, and_14_out, and_15_out, and_16_out, and_17_out, and_18_out,
       and_19_out, and_20_out, and_21_out, and_22_out, and_23_out, and_24_out, not_1_out, not_2_out,
       not_3_out, not_4_out, not_5_out, not_6_out, not_7_out, not_8_out, not_9_out, not_10_out, not_11_out,
       not_12_out, not_13_out, not_14_out, not_15_out, not_16_out, not_17_out, not_18_out, not_19_out,
       not_20_out, not_21_out, not_22_out, not_23_out, not_24_out, not_25_out, not_26_out, not_27_out,
       not_28_out, not_29_out, not_30_out, not_31_out, not_32_out, not_33_out, not_34_out, not_35_out,
       not_36_out, not_37_out, not_38_out, not_39_out;

  not not_1 (not_1_out, c5);
  not not_2 (not_2_out, c4);
  not not_3 (not_3_out, c2);
  not not_4 (not_4_out, c0);
  not not_5 (not_5_out, c4);
  not not_6 (not_6_out, c2);
  not not_7 (not_7_out, c2);
  not not_8 (not_8_out, c5);
  not not_9 (not_9_out, c3);
  not not_10 (not_10_out, c2);
  not not_11 (not_11_out, c5);
  not not_12 (not_12_out, c2);
  not not_13 (not_13_out, c0);
  not not_14 (not_14_out, c4);
  not not_15 (not_15_out, c1);
  not not_16 (not_16_out, c0);
  not not_17 (not_17_out, c4);
  not not_18 (not_18_out, c4);
  not not_19 (not_19_out, c2);
  not not_20 (not_20_out, c5);
  not not_21 (not_21_out, c2);
  not not_22 (not_22_out, c3);
  not not_23 (not_23_out, c2);
  not not_24 (not_24_out, c1);
  not not_25 (not_25_out, c0);
  not not_26 (not_26_out, c3);
  not not_27 (not_27_out, c2);
  not not_28 (not_28_out, c4);
  not not_29 (not_29_out, c3);
  not not_30 (not_30_out, c4);
  not not_31 (not_31_out, c3);
  not not_32 (not_32_out, c4);
  not not_33 (not_33_out, c0);
  not not_34 (not_34_out, c4);
  not not_35 (not_35_out, c5);
  not not_36 (not_36_out, c2);
  not not_37 (not_37_out, c3);
  not not_38 (not_38_out, c0);
  not not_39 (not_39_out, c0);
  and and_1 (a4, not_1_out, not_2_out);
  and and_2 (and_2_out, c5, not_3_out, not_4_out);
  and and_3 (and_3_out, c5, not_5_out, c2);
  and and_4 (and_4_out, c5, c3, not_6_out);
  and and_5 (and_5_out, c5, c4, not_7_out);
  and and_6 (and_6_out, not_8_out, not_9_out, not_10_out);
  and and_7 (and_7_out, not_11_out, c4, not_12_out, not_13_out);
  and and_8 (and_8_out, c5, not_14_out, c2, not_15_out, not_16_out);
  and and_9 (and_9_out, c5, not_17_out, c3);
  and and_10 (and_10_out, c5, c3, c2);
  and and_11 (and_11_out, not_18_out, c3, not_19_out);
  and and_12 (and_12_out, not_20_out, c3, not_21_out, c0);
  and and_13 (and_13_out, c4, not_22_out, not_23_out, not_24_out, not_25_out);
  and and_14 (and_14_out, c4, c3, c2);
  and and_15 (and_15_out, c5, not_26_out, not_27_out);
  and and_16 (and_16_out, c5, not_28_out, not_29_out, c0);
  and and_17 (and_17_out, c5, not_30_out, not_31_out, c1);
  and and_18 (and_18_out, not_32_out, c3, not_33_out);
  and and_19 (and_19_out, not_34_out, c3, c2);
  and and_20 (and_20_out, not_35_out, c4, not_36_out, c0);
  and and_21 (and_21_out, c4, not_37_out, c2, not_38_out);
  and and_22 (and_22_out, c5, c2, c0);
  and and_23 (and_23_out, c5, c2, c1);
  and and_24 (and_24_out, c5, c3, not_39_out);
  or or_1 (a3, and_2_out, and_3_out, and_4_out, and_5_out);
  or or_2 (a2, and_6_out, and_7_out, and_8_out, and_9_out, and_10_out);
  or or_3 (a1, and_11_out, and_12_out, and_13_out, and_14_out, and_15_out, and_16_out, and_17_out);
  or or_4 (a0, and_18_out, and_19_out, and_20_out, and_21_out, and_22_out, and_23_out, and_24_out);
endmodule

module concat (
  input  a0,
  input  a1,
  input  a2,
  input  a3,
  input  a4,
  output [4:0] aa
);

  wire [4:0] adder_1_out, adder_2_out, adder_3_out, bit_extender_1_out, bit_extender_2_out,
       bit_extender_3_out, bit_extender_4_out, bit_extender_5_out, shifter_1_out, shifter_2_out,
       shifter_3_out, shifter_4_out;

  assign bit_extender_1_out = {{4{1'b0}}, a0};  // Bit_Extender bit_extender_1
  assign bit_extender_2_out = {{4{1'b0}}, a1};  // Bit_Extender bit_extender_2
  assign bit_extender_3_out = {{4{1'b0}}, a2};  // Bit_Extender bit_extender_3
  assign bit_extender_4_out = {{4{1'b0}}, a3};  // Bit_Extender bit_extender_4
  assign bit_extender_5_out = {{4{1'b0}}, a4};  // Bit_Extender bit_extender_5
  Shifter #(.width(5)) shifter_1 (.in(bit_extender_2_out), .\dist (3'b001), .out(shifter_1_out));
  Shifter #(.width(5)) shifter_2 (.in(bit_extender_3_out), .\dist (3'b010), .out(shifter_2_out));
  Shifter #(.width(5)) shifter_3 (.in(bit_extender_4_out), .\dist (3'b011), .out(shifter_3_out));
  Shifter #(.width(5)) shifter_4 (.in(bit_extender_5_out), .\dist (3'b100), .out(shifter_4_out));
  Adder #(.width(5)) adder_1 (.a(bit_extender_1_out), .b(shifter_1_out), .out(adder_1_out));  // open: cin, cout
  Adder #(.width(5)) adder_2 (.a(shifter_2_out), .b(shifter_3_out), .out(adder_2_out));  // open: cin, cout
  Adder #(.width(5)) adder_3 (.a(adder_2_out), .b(shifter_4_out), .out(adder_3_out));  // open: cin, cout
  Adder #(.width(5)) adder_4 (.a(adder_1_out), .b(adder_3_out), .out(aa));  // open: cin, cout
endmodule
