// Logisim project da1_task4.circ as structural Verilog: 3 circuits, main circuit DUT
module DUT (
  input  [4:0] P,
  input  [4:0] K,
  output [4:0] C
);

  cipher cipher_1 (.P(P), .K(K), .C(C));

  // Notes on the sheet:
  //   Please put your deisgn below. You may also use subcircuits.
  //   However, do not move or rename any pins.
endmodule

module TB (
  input  [4:0] P,
  input  [4:0] K,
  output [4:0] C
);

  DUT dut_1 (.P(P), .K(K), .C(C));

  // Notes on the sheet:
  //   DO NOT MODIFY THIS
  //   TEST YOUR CIRCUITS USING THIS TO MAKE SURE YOU HAVE NOT ALTERED PIN OUT
endmodule

module cipher (
  input  [4:0] P,
  input  [4:0] K,
  output [4:0] C
);

  wire comparator_1_gt, not_1_out;
  wire [5:0] adder_1_out, adder_2_out, and_1_out, and_2_out, bit_extender_1_out, bit_extender_2_out,
       bit_extender_3_out, bit_extender_4_out, or_1_out, subtractor_1_out;

  assign bit_extender_1_out = {{1{1'b0}}, P};  // Bit_Extender bit_extender_1
  assign bit_extender_2_out = {{1{1'b0}}, K};  // Bit_Extender bit_extender_2
  Adder #(.width(6)) adder_1 (.a(bit_extender_1_out), .b(bit_extender_2_out), .out(adder_1_out));  // open: cin, cout
  // Probe on adder_2_out
  Adder #(.width(6)) adder_2 (.a(bit_extender_1_out), .b(bit_extender_2_out), .out(adder_2_out));  // open: cin, cout
  Comparator #(.width(6), .mode("unsigned")) comparator_1 (
    .a(adder_1_out), .b(6'b011001), .gt(comparator_1_gt));  // open: eq, lt
  // Probe on subtractor_1_out
  Subtractor #(.width(6)) subtractor_1 (.a(adder_2_out), .b(6'b011010), .out(subtractor_1_out));  // open: bin, bout
  assign bit_extender_3_out = {{5{comparator_1_gt}}, comparator_1_gt};  // Bit_Extender bit_extender_3
  not not_1 (not_1_out, comparator_1_gt);
  assign bit_extender_4_out = {{5{not_1_out}}, not_1_out};  // Bit_Extender bit_extender_4
  assign and_1_out = subtractor_1_out & bit_extender_3_out;  // AND_Gate and_1, 6 bits wide
  // Probe on and_1_out
  assign and_2_out = bit_extender_4_out & adder_2_out;  // AND_Gate and_2, 6 bits wide
  assign or_1_out = and_1_out | and_2_out;  // OR_Gate or_1, 6 bits wide
  BitSelector #(.width(6), .group(5)) bitselector_1 (.in(or_1_out), .out(C), .sel(1'b0));

  // Notes on the sheet:
  //   overflow
endmodule
