// Logisim project da1_task5.circ as structural Verilog: 3 circuits, main circuit DUT
module DUT (
  input  [3:0] D1,
  input  [3:0] D0,
  output [6:0] Z
);

  converter converter_1 (.D1(D1), .D0(D0), .Z(Z));

  // Notes on the sheet:
  //   Please put your deisgn below. You may also use subcircuits.
  //   However, do not move or rename any pins.
endmodule

module TB (
  input  [3:0] D1,
  input  [3:0] D0,
  output [6:0] Z
);

  DUT dut_1 (.D1(D1), .D0(D0), .Z(Z));

  // Notes on the sheet:
  //   DO NOT MODIFY THIS
  //   TEST YOUR CIRCUITS USING THIS TO MAKE SURE YOU HAVE NOT ALTERED PIN OUT
endmodule

module converter (
  input  [3:0] D1,
  input  [3:0] D0,
  output [6:0] Z
);

  wire [6:0] adder_1_out, bit_extender_1_out, bit_extender_2_out, shifter_1_out, shifter_2_out;

  assign bit_extender_1_out = {{3{1'b0}}, D1};  // Bit_Extender bit_extender_1
  assign bit_extender_2_out = {{3{1'b0}}, D0};  // Bit_Extender bit_extender_2
  Shifter #(.width(7)) shifter_1 (.in(bit_extender_1_out), .\dist (3'b001), .out(shifter_1_out));
  Shifter #(.width(7)) shifter_2 (.in(bit_extender_1_out), .\dist (3'b011), .out(shifter_2_out));
  Adder #(.width(7)) adder_1 (.a(shifter_1_out), .b(shifter_2_out), .out(adder_1_out));  // open: cin, cout
  Adder #(.width(7)) adder_2 (.a(adder_1_out), .b(bit_extender_2_out), .out(Z));  // open: cin, cout
endmodule
