// Logisim project da2_task1.circ as structural Verilog: 5 circuits, main circuit DUT
module DUT (
  input  DIN,
  input  CLK,
  input  RST,
  output DOUT
);

  main main_1 (.DIN(DIN), .RST(RST), .CLK(CLK), .DOUT(DOUT));

  // Notes on the sheet:
  //   Please put your deisgn below. You may also use subcircuits.
  //   However, do not move, rename, add, or delete any pins.
  //   Put your design below and wire it up to the pins.
  //   Feel free to remove this text.
endmodule

module TB (
);

  wire BUTTON_1_out, clk_out, dut_1_dout, pwr_on_reset_1_rst, t_ff_1_q;

  Clock sysclk ();  // open: out
  Button BUTTON_1 (.out(BUTTON_1_out));
  Clock #(.highDuration(2), .lowDuration(2)) clk (.out(clk_out));
  pwr_on_reset pwr_on_reset_1 (.CLK(clk_out), .RST(pwr_on_reset_1_rst));
  T_Flip_Flop t_ff_1 (.T(dut_1_dout), .clk(clk_out), .Q(t_ff_1_q));  // open: Qn, reset, preset
  DUT dut_1 (.DIN(BUTTON_1_out), .CLK(clk_out), .RST(pwr_on_reset_1_rst), .DOUT(dut_1_dout));
  LED LED1 (.in(t_ff_1_q));

  // Notes on the sheet:
  //   DO NOT MODIFY THIS
  //   YOU MAY TEST YOUR CIRCUITS USING THIS TO MAKE SURE YOU HAVE NOT ALTERED PIN OUT
  //   LED1 will toggle every clock tick that output of test circuit is high.
endmodule

module pwr_on_reset (
  input  CLK,
  output RST
);

  wire d_ff_1_q, nor_1_out, not_1_out;

  not not_1 (not_1_out, nor_1_out);
  D_Flip_Flop d_ff_1 (.D(not_1_out), .clk(CLK), .Q(d_ff_1_q));  // open: Qn, preset, reset
  D_Flip_Flop d_ff_2 (.D(nor_1_out), .clk(CLK), .Q(RST));  // open: Qn, preset, reset
  nor nor_1 (nor_1_out, d_ff_1_q, RST);

  // Notes on the sheet:
  //   DO NOT MODIFY THIS
endmodule

module main (
  input  DIN,
  input  RST,
  input  CLK,
  output DOUT
);

  wire and_1_out, and_2_out, d_ff_2_q, not_1_out, not_2_out, or_1_out;

  not not_1 (not_1_out, RST);
  and and_1 (and_1_out, not_2_out, DIN, ~d_ff_2_q, not_1_out);  // AND_Gate
  or or_1 (or_1_out, d_ff_2_q, DOUT);
  not not_2 (not_2_out, DOUT);
  D_Flip_Flop d_ff_1 (.D(and_1_out), .clk(CLK), .Q(DOUT));  // open: Qn, preset, reset
  D_Flip_Flop d_ff_2 (.D(and_2_out), .clk(CLK), .Q(d_ff_2_q));  // open: Qn, preset, reset
  and and_2 (and_2_out, or_1_out, not_1_out, DIN);
endmodule

module test (
  input  in_1
);

  wire button_1_out, clock_1_out, main_1_dout;

  Button button_1 (.out(button_1_out));
  Clock clock_1 (.out(clock_1_out));
  main main_1 (.DIN(button_1_out), .RST(in_1), .CLK(clock_1_out), .DOUT(main_1_dout));
  LED led_1 (.in(main_1_dout));
endmodule
