// Logisim project da2_task2.circ as structural Verilog: 9 circuits, main circuit DUT
module DUT (
  input  DIN,
  input  CLK,
  input  RST,
  output DOUT_SHORT,
  output DOUT_LONG
);

  main2 main2_1 (.DIN(DIN), .CLK(CLK), .RST(RST), .LONG(DOUT_SHORT), .SHORT(DOUT_LONG));

  // Notes on the sheet:
  //   Please put your deisgn below. You may also use subcircuits.
  //   However, do not move, rename, add, or delete any pins.
  //   Put your design below and wire it up to the pins.
  //   Feel free to remove this text.
endmodule

module TB (
);

  wire BUTTON_1_out, clk_out, dut_1_dout_long, dut_1_dout_short, pwr_on_reset_1_rst, t_ff_1_q, t_ff_2_q;

  Clock sysclk ();  // open: out
  Button BUTTON_1 (.out(BUTTON_1_out));
  Clock #(.highDuration(2), .lowDuration(2)) clk (.out(clk_out));
  pwr_on_reset pwr_on_reset_1 (.CLK(clk_out), .RST(pwr_on_reset_1_rst));
  T_Flip_Flop t_ff_1 (.T(dut_1_dout_short), .clk(clk_out), .Q(t_ff_1_q));  // open: Qn, reset, preset
  DUT dut_1 (
    .DIN(BUTTON_1_out), .CLK(clk_out), .RST(pwr_on_reset_1_rst), .DOUT_SHORT(dut_1_dout_short),
    .DOUT_LONG(dut_1_dout_long));
  LED LED1 (.in(t_ff_1_q));
  T_Flip_Flop t_ff_2 (.T(dut_1_dout_long), .clk(clk_out), .Q(t_ff_2_q));  // open: Qn, reset, preset
  LED LED2 (.in(t_ff_2_q));

  // Notes on the sheet:
  //   DO NOT MODIFY THIS
  //   YOU MAY TEST YOUR CIRCUITS USING THIS TO MAKE SURE YOU HAVE NOT ALTERED PIN OUT
  //   LED1 and LED2 will toggle every clock tick that the corresponding output of test circuit is high.
endmodule

module pwr_on_reset (
  input  CLK,
  output RST
);

  wire d_ff_1_q, nor_1_out, not_1_out;

  not not_1 (not_1_out, nor_1_out);
  D_Flip_Flop d_ff_1 (.D(not_1_out), .clk(CLK), .Q(d_ff_1_q));  // open: Qn, preset, reset
  D_Flip_Flop d_ff_2 (.D(nor_1_out), .clk(CLK), .Q(RST));  // open: Qn, preset, reset
  nor nor_1 (nor_1_out, d_ff_1_q, RST);

  // Notes on the sheet:
  //   DO NOT MODIFY THIS
endmodule

module main (
  input  DIN,
  input  CLK,
  input  RST,
  output DOUT_SHORT,
  output DOUT_LONG
);

  wire and_1_out, and_3_out, counter_1_carry, d_ff_1_q, n_DIN, not_2_out, not_3_out, not_4_out, start;
  wire [3:0] bit_extender_1_out;

  not not_1 (n_DIN, DIN);
  not not_2 (not_2_out, RST);
  not not_3 (not_3_out, d_ff_1_q);
  and and_1 (and_1_out, not_3_out, DIN, not_2_out);
  D_Flip_Flop d_ff_1 (.D(and_1_out), .clk(CLK), .Q(d_ff_1_q));  // open: Qn, preset, reset
  and and_2 (start, n_DIN, CLK);
  and and_3 (and_3_out, DIN, CLK);
  assign bit_extender_1_out = {{3{1'b0}}, d_ff_1_q};  // Bit_Extender bit_extender_1
  Counter #(.width(4), .max('h8), .ongoal("stay")) counter_1 (
    .clr(start), .clk(and_3_out), .D(bit_extender_1_out), .carry(counter_1_carry));  // open: load, up, count, Q
  not not_4 (not_4_out, counter_1_carry);
  lightOnce lightonce_1 (.in_1(counter_1_carry), .out_2(DOUT_LONG));
  lightOnce lightonce_2 (.in_1(not_4_out), .out_2(DOUT_SHORT));
endmodule

module test (
  input  RST
);

  wire CLK_out, DIN_out, main2_1_long, main2_1_short;

  Button DIN (.out(DIN_out));
  Clock CLK (.out(CLK_out));
  main2 main2_1 (.DIN(DIN_out), .CLK(CLK_out), .RST(RST), .LONG(main2_1_long), .SHORT(main2_1_short));
  LED long (.in(main2_1_long));
  LED short (.in(main2_1_short));
endmodule

module max (
  input  [2:0] in1,
  input  [2:0] in2,
  output [2:0] max
);

  wire comparator_1_gt, not_1_out;
  wire [2:0] and_1_out, and_2_out, bit_extender_1_out, bit_extender_2_out;

  Comparator #(.width(3), .mode("unsigned")) comparator_1 (.a(in1), .b(in2), .gt(comparator_1_gt));  // open: eq, lt
  assign bit_extender_1_out = {{2{comparator_1_gt}}, comparator_1_gt};  // Bit_Extender bit_extender_1
  // Probe on bit_extender_1_out
  not not_1 (not_1_out, comparator_1_gt);
  assign and_1_out = in1 & bit_extender_1_out;  // AND_Gate and_1, 3 bits wide
  assign bit_extender_2_out = {{2{not_1_out}}, not_1_out};  // Bit_Extender bit_extender_2
  // Probe on and_1_out
  assign and_2_out = bit_extender_2_out & in2;  // AND_Gate and_2, 3 bits wide
  assign max = and_1_out | and_2_out;  // OR_Gate or_1, 3 bits wide
endmodule

module simple_light (
  input  DIN,
  input  RST,
  input  CLK,
  output light
);

  wire and_1_out, and_2_out, d_ff_2_q, not_1_out, not_2_out, or_1_out;

  not not_1 (not_1_out, RST);
  and and_1 (and_1_out, not_2_out, DIN, ~d_ff_2_q, not_1_out);  // AND_Gate
  or or_1 (or_1_out, d_ff_2_q, light);
  not not_2 (not_2_out, light);
  D_Flip_Flop d_ff_1 (.D(and_1_out), .clk(CLK), .Q(light));  // open: Qn, preset, reset
  D_Flip_Flop d_ff_2 (.D(and_2_out), .clk(CLK), .Q(d_ff_2_q));  // open: Qn, preset, reset
  and and_2 (and_2_out, or_1_out, not_1_out, DIN);
endmodule

module lightOnce (
  input  in_1,
  output out_2
);

  buf and_1 (out_2, in_1);  // AND_Gate
endmodule

module main2 (
  input  DIN,
  input  CLK,
  input  RST,
  output LONG,
  output SHORT
);

  wire and_4_out, and_6_out, and_7_out, and_9_out, and_10_out, and_11_out, and_12_out, and_14_out, err_out,
       next0, next1, next2, next3, not_2_out, not_3_out, not_4_out, not_5_out, not_6_out, not_7_out,
       not_8_out, not_9_out, not_10_out, or_1_out, or_2_out, or_3_out, or_4_out, or_5_out, or_6_out,
       or_7_out, or_8_out, rst_t, s0, s1, s2, s3;

  not not_1 (rst_t, RST);
  D_Flip_Flop d_ff_1 (.D(next0), .clk(CLK), .Q(s0));  // open: Qn, preset, reset
  D_Flip_Flop d_ff_2 (.D(next1), .clk(CLK), .Q(s1));  // open: Qn, preset, reset
  D_Flip_Flop d_ff_3 (.D(next2), .clk(CLK), .Q(s2));  // open: Qn, preset, reset
  D_Flip_Flop d_ff_4 (.D(next3), .clk(CLK), .Q(s3));  // open: Qn, preset, reset
  and and_1 (LONG, s0, s3);
  and and_2 (SHORT, s1, s3);
  or or_1 (or_1_out, s2, s1);
  or or_2 (or_2_out, s2, s0);
  and and_3 (next2, DIN, or_1_out, or_2_out, or_3_out, rst_t);
  or or_3 (or_3_out, ~s2, ~s1, ~s0);  // OR_Gate
  and and_4 (and_4_out, s3, s0, DIN);
  not not_2 (not_2_out, DIN);
  not not_3 (not_3_out, s0);
  and err (err_out, DIN, s1, not_3_out);
  and and_5 (next0, rst_t, or_7_out);
  or or_4 (or_4_out, ~s0, ~s1, not_2_out);  // OR_Gate
  or or_5 (or_5_out, not_2_out, s0, s1);
  or or_6 (or_6_out, s1, s0, s2);
  not not_4 (not_4_out, s1);
  not not_5 (not_5_out, s3);
  and and_6 (and_6_out, not_5_out, not_3_out, DIN);
  or or_7 (or_7_out, and_4_out, err_out, and_6_out, and_7_out);
  not not_6 (not_6_out, DIN);
  and and_7 (and_7_out, s3, not_4_out, not_3_out, not_6_out);
  and and_8 (next1, rst_t, or_4_out, or_5_out, or_6_out, ~s3);  // AND_Gate
  not not_7 (not_7_out, DIN);
  and and_9 (and_9_out, s2, not_7_out);
  and and_10 (and_10_out, s2, s1, s0);
  not not_8 (not_8_out, s3);
  and and_11 (and_11_out, s0, not_7_out, not_8_out);
  and and_12 (and_12_out, s1, not_7_out, not_8_out);
  or or_8 (or_8_out, and_9_out, and_10_out, and_11_out, and_12_out, and_14_out);
  and and_13 (next3, rst_t, or_8_out);
  not not_9 (not_9_out, s0);
  not not_10 (not_10_out, s1);
  and and_14 (and_14_out, s3, not_10_out, not_9_out);
endmodule
