// Logisim project da2_task3.circ as structural Verilog: 4 circuits, main circuit DUT
module DUT (
  input  DIN,
  input  CLK,
  input  RST,
  output DOUT
);

  main main_1 (.DIN(DIN), .CLK(CLK), .RST(RST), .DOUT(DOUT));

  // Notes on the sheet:
  //   Please put your deisgn below. You may also use subcircuits.
  //   However, do not move, rename, add, or delete any pins.
  //   Put your design below and wire it up to the pins.
  //   Feel free to remove this text.
endmodule

module TB (
);

  wire clk_out, pwr_on_reset_1_rst;
  wire [0:0] dut_1_dout, random_1_out;

  Clock sysclk ();  // open: out
  Random #(.width(1)) random_1 (.clk(clk_out), .out(random_1_out[0]));  // open: clr, next
  Clock #(.highDuration(2), .lowDuration(2)) clk (.out(clk_out));
  pwr_on_reset pwr_on_reset_1 (.CLK(clk_out), .RST(pwr_on_reset_1_rst));
  LED led_1 (.in(random_1_out[0]));
  DUT dut_1 (.DIN(random_1_out[0]), .CLK(clk_out), .RST(pwr_on_reset_1_rst), .DOUT(dut_1_dout[0]));
  TTY #(.rows(4)) tty_1 (.data({6'b011000, dut_1_dout[0]}), .clk(clk_out));  // open: we, clr
  TTY #(.rows(4)) tty_2 (.data({6'b011000, random_1_out[0]}), .clk(clk_out));  // open: we, clr

  // Notes on the sheet:
  //   DO NOT MODIFY THIS
  //   YOU MAY TEST YOUR CIRCUITS USING THIS TO MAKE SURE YOU HAVE NOT ALTERED PIN OUT
  //   Top screen shows output, bottom screen shows the random input.
endmodule

module pwr_on_reset (
  input  CLK,
  output RST
);

  wire d_ff_1_q, nor_1_out, not_1_out;

  not not_1 (not_1_out, nor_1_out);
  D_Flip_Flop d_ff_1 (.D(not_1_out), .clk(CLK), .Q(d_ff_1_q));  // open: Qn, preset, reset
  D_Flip_Flop d_ff_2 (.D(nor_1_out), .clk(CLK), .Q(RST));  // open: Qn, preset, reset
  nor nor_1 (nor_1_out, d_ff_1_q, RST);

  // Notes on the sheet:
  //   DO NOT MODIFY THIS
endmodule

module main (
  input  DIN,
  input  CLK,
  input  RST,
  output DOUT
);

  wire and_1_out, and_2_out, and_3_out, and_4_out, and_5_out, and_6_out, next1, next2, not_2_out, not_3_out,
       or_1_out, or_2_out, or_3_out, rst_t, s1, s2, s3;

  not not_1 (rst_t, RST);
  D_Flip_Flop d_ff_1 (.D(next1), .clk(CLK), .Q(s1));  // open: Qn, preset, reset
  D_Flip_Flop d_ff_2 (.D(next2), .clk(CLK), .Q(s2));  // open: Qn, preset, reset
  D_Flip_Flop d_ff_3 (.D(DIN), .clk(CLK), .Q(s3));  // open: Qn, preset, reset
  not not_2 (not_2_out, DIN);
  not not_3 (not_3_out, s2);
  and and_1 (and_1_out, not_2_out, s1, s2);
  and and_2 (and_2_out, not_2_out, ~s1, ~s2, ~s3);  // AND_Gate
  or or_1 (or_1_out, and_1_out, and_2_out);
  and and_3 (and_3_out, ~s1, s2, ~s3);  // AND_Gate
  or or_2 (or_2_out, and_3_out, and_4_out);
  and and_4 (and_4_out, s1, ~s2, s3);  // AND_Gate
  and and_5 (and_5_out, s1, not_3_out, ~s3);  // AND_Gate
  and and_6 (and_6_out, ~s1, not_3_out, s3);  // AND_Gate
  and and_7 (DOUT, rst_t, or_1_out);
  and and_8 (next1, rst_t, or_2_out);
  and and_9 (next2, rst_t, or_3_out);
  or or_3 (or_3_out, and_5_out, and_6_out);

  // Other names for the same wires on the sheet: next3 = DIN
endmodule
