// Logisim project da2_task4.circ as structural Verilog: 15 circuits, main circuit DUT
module DUT (
  input  [6:0] DIN,
  input  RDY,
  input  CLK,
  input  RST,
  output F
);

  main main_1 (.DIN(DIN), .RDY(RDY), .CLK(CLK), .RST(RST), .F(F));

  // Notes on the sheet:
  //   Please put your deisgn below. You may also use subcircuits.
  //   However, do not move, rename, add, or delete any pins.
  //   Put your design below and wire it up to the pins.
  //   Feel free to remove this text.
endmodule

module TB (
);

  wire clk_out, keyboard_1_avail, pwr_on_reset_1_rst;
  wire [0:0] dut_1_f;
  wire [6:0] keyboard_1_data;

  Keyboard keyboard_1 (.clk(clk_out), .avail(keyboard_1_avail), .data(keyboard_1_data));  // open: re, clr
  Clock #(.highDuration(2), .lowDuration(2)) clk (.out(clk_out));
  Clock sysclk ();  // open: out
  pwr_on_reset pwr_on_reset_1 (.CLK(clk_out), .RST(pwr_on_reset_1_rst));
  DUT dut_1 (.DIN(keyboard_1_data), .RDY(keyboard_1_avail), .CLK(clk_out), .RST(pwr_on_reset_1_rst), .F(dut_1_f[0]));
  TTY tty_1 (.data(keyboard_1_data), .clk(clk_out));  // open: we, clr
  TTY tty_2 (.data({6'b011000, dut_1_f[0]}), .clk(clk_out));  // open: we, clr

  // Notes on the sheet:
  //   DO NOT MODIFY THIS
  //   YOU MAY TEST YOUR CIRCUITS USING THIS TO MAKE SURE YOU HAVE NOT ALTERED PIN OUT
  //   Top display will show what was typed thus far
  //   Bottom display will show output F
endmodule

module pwr_on_reset (
  input  CLK,
  output RST
);

  wire d_ff_1_q, nor_1_out, not_1_out;

  not not_1 (not_1_out, nor_1_out);
  D_Flip_Flop d_ff_1 (.D(not_1_out), .clk(CLK), .Q(d_ff_1_q));  // open: Qn, preset, reset
  D_Flip_Flop d_ff_2 (.D(nor_1_out), .clk(CLK), .Q(RST));  // open: Qn, preset, reset
  nor nor_1 (nor_1_out, d_ff_1_q, RST);

  // Notes on the sheet:
  //   DO NOT MODIFY THIS
endmodule

module main (
  input  [6:0] DIN,
  input  RDY,
  input  CLK,
  input  RST,
  output F
);

  wire a_1_out_2, a_2_out_2, and_1_out, and_3_out, and_4_out, and_5_out, and_6_out, and_7_out, and_8_out,
       and_9_out, and_10_out, and_11_out, and_12_out, and_13_out, and_14_out, and_15_out, and_16_out,
       and_17_out, and_18_out, and_19_out, and_20_out, and_21_out, and_22_out, and_23_out, and_24_out,
       and_25_out, and_27_out, and_28_out, and_29_out, and_30_out, and_32_out, and_33_out, and_34_out,
       and_35_out, and_36_out, and_37_out, and_38_out, and_39_out, c_1_out_2, c_2_out_2, c_3_out_2,
       c_4_out_2, d_1_out_2, d_2_out_2, i_1_out_2, i_2_out_2, i_3_out_2, i_4_out_2, invalid_1_out_2,
       n_1_out_2, n_2_out_2, n_RDY, next0, next1, next2, next3, next4, next5, next6, next7, next8, next9,
       next10, next11, next12, next13, next14, o_1_out_2, o_2_out_2, o_3_out_2, o_4_out_2, or_1_out,
       r_1_out_2, r_2_out_2, r_3_out_2, r_4_out_2, r_5_out_2, r_6_out_2, rst_t, s0, s1, s2, s3, s4, s5, s6,
       s7, s8, s9, s10, s11, s12, s13, s14, s_1_out_2, s_2_out_2, u_1_out_2, u_2_out_2, undriven, v_1_out_2,
       v_2_out_2, v_3_out_2, v_4_out_2, v_5_out_2, v_6_out_2;

  not not_1 (n_RDY, RDY);
  not not_2 (rst_t, RST);
  D_Flip_Flop d_ff_1 (.D(next0), .clk(CLK), .Q(s0));  // open: Qn, preset, reset
  D_Flip_Flop d_ff_2 (.D(next1), .clk(CLK), .Q(s1));  // open: Qn, preset, reset
  D_Flip_Flop d_ff_3 (.D(next2), .clk(CLK), .Q(s2));  // open: Qn, preset, reset
  D_Flip_Flop d_ff_4 (.D(next3), .clk(CLK), .Q(s3));  // open: Qn, preset, reset
  D_Flip_Flop d_ff_5 (.D(next4), .clk(CLK), .Q(s4));  // open: Qn, preset, reset
  D_Flip_Flop d_ff_6 (.D(next5), .clk(CLK), .Q(s5));  // open: Qn, preset, reset
  D_Flip_Flop d_ff_7 (.D(next6), .clk(CLK), .Q(s6));  // open: Qn, preset, reset
  D_Flip_Flop d_ff_8 (.D(next7), .clk(CLK), .Q(s7));  // open: Qn, preset, reset
  D_Flip_Flop d_ff_9 (.D(next8), .clk(CLK), .Q(s8));  // open: Qn, preset, reset
  D_Flip_Flop d_ff_10 (.D(next9), .clk(CLK), .Q(s9));  // open: Qn, preset, reset
  D_Flip_Flop d_ff_11 (.D(next10), .clk(CLK), .Q(s10));  // open: Qn, preset, reset
  D_Flip_Flop d_ff_12 (.D(next11), .clk(CLK), .Q(s11));  // open: Qn, preset, reset
  D_Flip_Flop d_ff_13 (.D(next12), .clk(CLK), .Q(s12), .reset(undriven));  // open: Qn, preset
  D_Flip_Flop d_ff_14 (.D(next13), .clk(CLK), .Q(s13));  // open: Qn, preset, reset
  D_Flip_Flop d_ff_15 (.D(next14), .clk(CLK), .Q(s14));  // open: Qn, preset, reset
  or or_1 (or_1_out, s6, s9, s14);
  and and_1 (and_1_out, s0, n_RDY);
  O o_1 (.in_1(DIN), .out_2(o_1_out_2));
  R r_1 (.in_1(DIN), .out_2(r_1_out_2));
  V v_1 (.in_1(DIN), .out_2(v_1_out_2));
  O o_2 (.in_1(DIN), .out_2(o_2_out_2));
  N n_1 (.in_1(DIN), .out_2(n_1_out_2));
  A a_1 (.in_1(DIN), .out_2(a_1_out_2));
  C c_1 (.in_1(DIN), .out_2(c_1_out_2));
  V v_2 (.in_1(DIN), .out_2(v_2_out_2));
  I i_1 (.in_1(DIN), .out_2(i_1_out_2));
  D d_1 (.in_1(DIN), .out_2(d_1_out_2));
  R r_2 (.in_1(DIN), .out_2(r_2_out_2));
  C c_2 (.in_1(DIN), .out_2(c_2_out_2));
  V v_3 (.in_1(DIN), .out_2(v_3_out_2));
  I i_2 (.in_1(DIN), .out_2(i_2_out_2));
  R r_3 (.in_1(DIN), .out_2(r_3_out_2));
  U u_1 (.in_1(DIN), .out_2(u_1_out_2));
  S s_1 (.in_1(DIN), .out_2(s_1_out_2));
  C c_3 (.in_1(DIN), .out_2(c_3_out_2));
  V v_4 (.in_1(DIN), .out_2(v_4_out_2));
  and and_2 (F, rst_t, or_1_out);
  invalid invalid_1 (.in_1(DIN), .out_2(invalid_1_out_2));
  and and_3 (and_3_out, s1, ~o_1_out_2);  // AND_Gate
  and and_4 (and_4_out, s2, ~r_1_out_2, ~v_1_out_2);  // AND_Gate
  and and_5 (and_5_out, s3, ~o_2_out_2);  // AND_Gate
  and and_6 (and_6_out, s4, ~n_1_out_2);  // AND_Gate
  and and_7 (and_7_out, s5, ~a_1_out_2);  // AND_Gate
  and and_8 (and_8_out, s6, ~c_1_out_2, ~v_2_out_2);  // AND_Gate
  and and_9 (and_9_out, s7, ~i_1_out_2);  // AND_Gate
  and and_10 (and_10_out, s8, ~d_1_out_2, ~r_2_out_2);  // AND_Gate
  and and_11 (and_11_out, s9, ~c_2_out_2, ~v_3_out_2);  // AND_Gate
  and and_12 (and_12_out, s10, ~i_2_out_2);  // AND_Gate
  and and_13 (and_13_out, s11, ~r_3_out_2);  // AND_Gate
  and and_14 (and_14_out, s12, ~u_1_out_2);  // AND_Gate
  and and_15 (and_15_out, s13, ~s_1_out_2);  // AND_Gate
  and and_16 (and_16_out, s14, ~c_3_out_2, ~v_4_out_2);  // AND_Gate
  or or_2 (next0, and_1_out, invalid_1_out_2, and_3_out, and_4_out, and_5_out, and_6_out, and_7_out, and_8_out, and_9_out, and_10_out, and_11_out, and_12_out, and_13_out, and_14_out, and_15_out, and_16_out);
  C c_4 (.in_1(DIN), .out_2(c_4_out_2));
  O o_3 (.in_1(DIN), .out_2(o_3_out_2));
  R r_4 (.in_1(DIN), .out_2(r_4_out_2));
  O o_4 (.in_1(DIN), .out_2(o_4_out_2));
  N n_2 (.in_1(DIN), .out_2(n_2_out_2));
  A a_2 (.in_1(DIN), .out_2(a_2_out_2));
  V v_5 (.in_1(DIN), .out_2(v_5_out_2));
  I i_3 (.in_1(DIN), .out_2(i_3_out_2));
  D d_2 (.in_1(DIN), .out_2(d_2_out_2));
  V v_6 (.in_1(DIN), .out_2(v_6_out_2));
  I i_4 (.in_1(DIN), .out_2(i_4_out_2));
  R r_5 (.in_1(DIN), .out_2(r_5_out_2));
  R r_6 (.in_1(DIN), .out_2(r_6_out_2));
  U u_2 (.in_1(DIN), .out_2(u_2_out_2));
  S s_2 (.in_1(DIN), .out_2(s_2_out_2));
  and and_17 (and_17_out, s1, n_RDY);
  or or_3 (next1, and_17_out, c_4_out_2);
  and and_18 (and_18_out, s2, n_RDY);
  or or_4 (next2, and_18_out, and_19_out);
  and and_19 (and_19_out, s1, o_3_out_2);
  and and_20 (and_20_out, s3, n_RDY);
  or or_5 (next3, and_20_out, and_21_out);
  and and_21 (and_21_out, s2, r_4_out_2);
  and and_22 (and_22_out, s4, n_RDY);
  or or_6 (next4, and_22_out, and_23_out);
  and and_23 (and_23_out, s3, o_4_out_2);
  and and_24 (and_24_out, s5, n_RDY);
  or or_7 (next5, and_24_out, and_25_out);
  and and_25 (and_25_out, s4, n_2_out_2);
  and and_26 (next6, s5, ~s6, a_2_out_2);  // AND_Gate
  and and_27 (and_27_out, s7, n_RDY);
  or or_8 (next7, and_27_out, and_28_out);
  and and_28 (and_28_out, s2, v_5_out_2);
  and and_29 (and_29_out, s8, n_RDY);
  or or_9 (next8, and_29_out, and_30_out);
  and and_30 (and_30_out, s7, i_3_out_2);
  and and_31 (next9, s8, ~s9, d_2_out_2);  // AND_Gate
  and and_32 (and_32_out, s10, n_RDY);
  and and_33 (and_33_out, s11, n_RDY);
  and and_34 (and_34_out, s10, i_4_out_2);
  and and_35 (and_35_out, s12, n_RDY);
  and and_36 (and_36_out, s11, r_5_out_2);
  and and_37 (and_37_out, s8, r_6_out_2);
  and and_38 (and_38_out, s13, n_RDY);
  and and_39 (and_39_out, s12, u_2_out_2);
  and and_40 (next14, s13, ~s14, s_2_out_2);  // AND_Gate
  or or_10 (next10, and_32_out, v_6_out_2);
  or or_11 (next11, and_33_out, and_34_out);
  or or_12 (next12, and_35_out, and_36_out, and_37_out);
  or or_13 (next13, and_38_out, and_39_out);
endmodule

module C (
  input  [6:0] in_1,
  output out_2
);

  wire comparator_1_eq, comparator_2_eq;

  Comparator #(.width(7), .mode("unsigned")) comparator_1 (
    .a(7'b1100011), .b(in_1), .eq(comparator_1_eq));  // open: gt, lt
  Comparator #(.width(7), .mode("unsigned")) comparator_2 (
    .a(in_1), .b(7'b1000011), .eq(comparator_2_eq));  // open: gt, lt
  or or_1 (out_2, comparator_1_eq, comparator_2_eq);
endmodule

module O (
  input  [6:0] in_1,
  output out_2
);

  wire comparator_1_eq, comparator_2_eq;

  Comparator #(.width(7), .mode("unsigned")) comparator_1 (
    .a(7'b1101111), .b(in_1), .eq(comparator_1_eq));  // open: gt, lt
  Comparator #(.width(7), .mode("unsigned")) comparator_2 (
    .a(in_1), .b(7'b1001111), .eq(comparator_2_eq));  // open: gt, lt
  or or_1 (out_2, comparator_1_eq, comparator_2_eq);
endmodule

module R (
  input  [6:0] in_1,
  output out_2
);

  wire comparator_1_eq, comparator_2_eq;

  Comparator #(.width(7), .mode("unsigned")) comparator_1 (
    .a(7'b1110010), .b(in_1), .eq(comparator_1_eq));  // open: gt, lt
  Comparator #(.width(7), .mode("unsigned")) comparator_2 (
    .a(in_1), .b(7'b1010010), .eq(comparator_2_eq));  // open: gt, lt
  or or_1 (out_2, comparator_1_eq, comparator_2_eq);
endmodule

module N (
  input  [6:0] in_1,
  output out_2
);

  wire comparator_1_eq, comparator_2_eq;

  Comparator #(.width(7), .mode("unsigned")) comparator_1 (
    .a(7'b1101110), .b(in_1), .eq(comparator_1_eq));  // open: gt, lt
  Comparator #(.width(7), .mode("unsigned")) comparator_2 (
    .a(in_1), .b(7'b1001110), .eq(comparator_2_eq));  // open: gt, lt
  or or_1 (out_2, comparator_1_eq, comparator_2_eq);
endmodule

module A (
  input  [6:0] in_1,
  output out_2
);

  wire comparator_1_eq, comparator_2_eq;

  Comparator #(.width(7), .mode("unsigned")) comparator_1 (
    .a(7'b1100001), .b(in_1), .eq(comparator_1_eq));  // open: gt, lt
  Comparator #(.width(7), .mode("unsigned")) comparator_2 (
    .a(in_1), .b(7'b1000001), .eq(comparator_2_eq));  // open: gt, lt
  or or_1 (out_2, comparator_1_eq, comparator_2_eq);
endmodule

module V (
  input  [6:0] in_1,
  output out_2
);

  wire comparator_1_eq, comparator_2_eq;

  Comparator #(.width(7), .mode("unsigned")) comparator_1 (
    .a(7'b1110110), .b(in_1), .eq(comparator_1_eq));  // open: gt, lt
  Comparator #(.width(7), .mode("unsigned")) comparator_2 (
    .a(in_1), .b(7'b1010110), .eq(comparator_2_eq));  // open: gt, lt
  or or_1 (out_2, comparator_1_eq, comparator_2_eq);
endmodule

module I (
  input  [6:0] in_1,
  output out_2
);

  wire comparator_1_eq, comparator_2_eq;

  Comparator #(.width(7), .mode("unsigned")) comparator_1 (
    .a(7'b1101001), .b(in_1), .eq(comparator_1_eq));  // open: gt, lt
  Comparator #(.width(7), .mode("unsigned")) comparator_2 (
    .a(in_1), .b(7'b1001001), .eq(comparator_2_eq));  // open: gt, lt
  or or_1 (out_2, comparator_1_eq, comparator_2_eq);
endmodule

module U (
  input  [6:0] in_1,
  output out_2
);

  wire comparator_1_eq, comparator_2_eq;

  Comparator #(.width(7), .mode("unsigned")) comparator_1 (
    .a(7'b1110101), .b(in_1), .eq(comparator_1_eq));  // open: gt, lt
  Comparator #(.width(7), .mode("unsigned")) comparator_2 (
    .a(in_1), .b(7'b1010101), .eq(comparator_2_eq));  // open: gt, lt
  or or_1 (out_2, comparator_1_eq, comparator_2_eq);
endmodule

module S (
  input  [6:0] in_1,
  output out_2
);

  wire comparator_1_eq, comparator_2_eq;

  Comparator #(.width(7), .mode("unsigned")) comparator_1 (
    .a(7'b1110011), .b(in_1), .eq(comparator_1_eq));  // open: gt, lt
  Comparator #(.width(7), .mode("unsigned")) comparator_2 (
    .a(in_1), .b(7'b1010011), .eq(comparator_2_eq));  // open: gt, lt
  or or_1 (out_2, comparator_1_eq, comparator_2_eq);
endmodule

module D (
  input  [6:0] in_1,
  output out_2
);

  wire comparator_1_eq, comparator_2_eq;

  Comparator #(.width(7), .mode("unsigned")) comparator_1 (
    .a(7'b1100100), .b(in_1), .eq(comparator_1_eq));  // open: gt, lt
  Comparator #(.width(7), .mode("unsigned")) comparator_2 (
    .a(in_1), .b(7'b1000100), .eq(comparator_2_eq));  // open: gt, lt
  or or_1 (out_2, comparator_1_eq, comparator_2_eq);
endmodule

module invalid (
  input  [6:0] in_1,
  output out_2
);

  wire a_1_out_2, c_1_out_2, d_1_out_2, i_1_out_2, n_1_out_2, o_1_out_2, r_1_out_2, s_1_out_2, u_1_out_2,
       v_1_out_2;

  C c_1 (.in_1(in_1), .out_2(c_1_out_2));
  O o_1 (.in_1(in_1), .out_2(o_1_out_2));
  R r_1 (.in_1(in_1), .out_2(r_1_out_2));
  N n_1 (.in_1(in_1), .out_2(n_1_out_2));
  A a_1 (.in_1(in_1), .out_2(a_1_out_2));
  V v_1 (.in_1(in_1), .out_2(v_1_out_2));
  I i_1 (.in_1(in_1), .out_2(i_1_out_2));
  U u_1 (.in_1(in_1), .out_2(u_1_out_2));
  S s_1 (.in_1(in_1), .out_2(s_1_out_2));
  D d_1 (.in_1(in_1), .out_2(d_1_out_2));
  nand nand_1 (out_2, c_1_out_2, o_1_out_2, r_1_out_2, n_1_out_2, a_1_out_2, v_1_out_2, i_1_out_2, u_1_out_2, s_1_out_2, d_1_out_2);
endmodule
