// Logisim project da3.circ as structural Verilog: 12 circuits, main circuit DUT
module DUT (
  input  CLK,
  input  RST,
  input  REQ,
  input  [15:0] A,
  input  [15:0] D,
  output ACK,
  output FDBZ,
  output [15:0] Q,
  output [15:0] R
);

  main main_1 (.CLK(CLK), .RST(RST), .REQ(REQ), .A(A), .D(D), .ACK(ACK), .FDBZ(FDBZ), .Q(Q), .R(R));

  // Notes on the sheet:
  //   Please put your deisgn below. You may also use subcircuits.
  //   However, do not move, rename, add, or delete any pins.
  //   Note that A, D, Q, and R in Hex
  //   Put your design below and wire it up to the pins using tunnels.
  //   Feel free to remove this text.
endmodule

module TB (
  input  [15:0] Dividend,
  input  [15:0] Divisor,
  input  REQ,
  output [15:0] Quotient,
  output [15:0] Remainder
);

  wire clock_1_out, Divider16bitSigned_ack, Divider16bitSigned_fdbz, pwr_on_reset_1_rst;

  Clock clock_1 (.out(clock_1_out));
  Clock sysclk ();  // open: out
  pwr_on_reset pwr_on_reset_1 (.CLK(clock_1_out), .RST(pwr_on_reset_1_rst));
  DUT Divider16bitSigned (
    .CLK(clock_1_out), .RST(pwr_on_reset_1_rst), .REQ(REQ), .A(Dividend), .D(Divisor),
    .ACK(Divider16bitSigned_ack), .FDBZ(Divider16bitSigned_fdbz), .Q(Quotient), .R(Remainder));
  LED ACK (.in(Divider16bitSigned_ack));
  LED DivideByZero (.in(Divider16bitSigned_fdbz));

  // Notes on the sheet:
  //   DO NOT MODIFY THIS
  //   YOU MAY TEST YOUR CIRCUITS USING THIS TO MAKE SURE YOU HAVE NOT ALTERED PIN OUT
  //   The multibit values are in Hexadeximal
endmodule

module pwr_on_reset (
  input  CLK,
  output RST
);

  wire d_ff_1_q, nor_1_out, not_1_out;

  not not_1 (not_1_out, nor_1_out);
  D_Flip_Flop d_ff_1 (.D(not_1_out), .clk(CLK), .Q(d_ff_1_q));  // open: Qn, preset, reset
  D_Flip_Flop d_ff_2 (.D(nor_1_out), .clk(CLK), .Q(RST));  // open: Qn, preset, reset
  nor nor_1 (nor_1_out, d_ff_1_q, RST);

  // Notes on the sheet:
  //   DO NOT MODIFY THIS
endmodule

module main (
  input  CLK,
  input  RST,
  input  REQ,
  input  [15:0] A,
  input  [15:0] D,
  output ACK,
  output FDBZ,
  output [15:0] Q,
  output [15:0] R
);

  wire and_3_out, and_4_out, and_5_out, comparator_1_eq, comparator_2_gt, comparator_3_lt, counter_1_carry,
       not_1_out, not_2_out, not_3_out, not_4_out, rst_t;
  wire [15:0] absval_1_abso, absval_2_abso, absval_3_abso, and_2_out, and_6_out, and_7_out, and_8_out,
       bit_extender_1_out, bit_extender_2_out, bit_extender_3_out, bit_extender_4_out, bit_extender_5_out,
       bit_extender_6_out, multiplier_1_out, or_2_out, q_normal, q_t, r_t, register_1_q, register_2_q,
       subtractor_1_out, test4_1_out_6;

  not not_1 (not_1_out, REQ);
  Counter #(.width(5), .max('h10), .ongoal("stay")) counter_1 (
    .carry(counter_1_carry), .up(REQ));  // open: load, D, count, Q, clk, clr
  or or_1 (counter_1_carry, not_1_out, rst_t);
  Multiplier #(.width(16)) multiplier_1 (.a(q_t), .b(D), .out(multiplier_1_out));  // open: cin, cout
  assign bit_extender_1_out = {{15{not_2_out}}, not_2_out};  // Bit_Extender bit_extender_1
  not not_2 (not_2_out, rst_t);
  D_Flip_Flop d_ff_1 (.D(RST), .clk(CLK), .Q(rst_t));  // open: Qn, preset, reset
  absVal absval_1 (.inp(A), .abso(absval_1_abso));
  absVal absval_2 (.inp(D), .abso(absval_2_abso));
  Subtractor #(.width(16)) subtractor_1 (.a(A), .b(multiplier_1_out), .out(subtractor_1_out));  // open: bin, bout
  absVal absval_3 (.inp(subtractor_1_out), .abso(absval_3_abso));
  Register #(.width(16)) register_1 (.D(q_t), .en(REQ), .clk(CLK), .Q(register_1_q));  // open: clr
  assign r_t = absval_3_abso & bit_extender_1_out;  // AND_Gate and_1, 16 bits wide
  test4 test4_1 (
    .A(absval_1_abso), .D(absval_2_abso), .req(REQ), .rst(rst_t), .clk(CLK), .out_6(test4_1_out_6), .ack(ACK));
  Multiplexer #(.width(16), .enable("false")) multiplexer_1 (.in0({16{1'b0}}), .in1(register_1_q), .out(Q), .sel(ACK));
  not not_3 (not_3_out, FDBZ);
  assign bit_extender_2_out = {{15{not_3_out}}, not_3_out};  // Bit_Extender bit_extender_2
  Comparator #(.width(16)) comparator_1 (.a(A), .b({16{1'b0}}), .eq(comparator_1_eq));  // open: gt, lt
  Comparator #(.width(16)) comparator_2 (.a(A), .b({16{1'b0}}), .gt(comparator_2_gt));  // open: eq, lt
  Comparator #(.width(16)) comparator_3 (.a(A), .b({16{1'b0}}), .lt(comparator_3_lt));  // open: gt, eq
  // Probe on test4_1_out_6
  Comparator #(.width(16)) comparator_4 (.a(D), .b({16{1'b0}}), .eq(FDBZ));  // open: gt, lt
  assign and_2_out = q_normal & bit_extender_2_out;  // AND_Gate and_2, 16 bits wide
  and and_3 (and_3_out, FDBZ, comparator_1_eq);
  assign bit_extender_3_out = {{15{and_3_out}}, and_3_out};  // Bit_Extender bit_extender_3
  and and_4 (and_4_out, FDBZ, comparator_2_gt);
  assign bit_extender_4_out = {{15{and_4_out}}, and_4_out};  // Bit_Extender bit_extender_4
  and and_5 (and_5_out, FDBZ, comparator_3_lt);
  assign bit_extender_5_out = {{15{and_5_out}}, and_5_out};  // Bit_Extender bit_extender_5
  getQ getq_1 (.A_all(A), .D_all(D), .Q(test4_1_out_6), .out_4(q_normal));
  // Probe on and_2_out
  assign and_6_out = bit_extender_3_out & {16{1'b0}};  // AND_Gate and_6, 16 bits wide
  assign and_7_out = bit_extender_4_out & 16'h7fff;  // AND_Gate and_7, 16 bits wide
  assign and_8_out = bit_extender_5_out & 16'h8000;  // AND_Gate and_8, 16 bits wide
  Register #(.width(16)) register_2 (.D(r_t), .en(REQ), .clk(CLK), .Q(register_2_q));  // open: clr
  // Probe on and_6_out
  assign or_2_out = and_2_out | and_6_out | and_7_out | and_8_out;  // OR_Gate or_2, 16 bits wide
  not not_4 (not_4_out, rst_t);
  Multiplexer #(.width(16), .enable("false")) multiplexer_2 (.in0({16{1'b0}}), .in1(register_2_q), .out(R), .sel(ACK));
  assign q_t = or_2_out & bit_extender_6_out;  // AND_Gate and_9, 16 bits wide
  assign bit_extender_6_out = {{15{not_4_out}}, not_4_out};  // Bit_Extender bit_extender_6

  // Other names for the same wires on the sheet: out_q[15:0] = Q; out_r[15:0] = R
endmodule

module positiveDivide (
  input  [15:0] A,
  input  [15:0] D,
  input  CLK,
  output [15:0] Q
);
endmodule

module getQ (
  input  [15:0] A_all,
  input  [15:0] D_all,
  input  [15:0] Q,
  output [15:0] out_4
);

  wire and_1_out, and_2_out, comparator_1_eq, not_2_out, xor_1_out;
  wire [15:0] a, adder_2_out, and_4_out, and_6_out, and_7_out, bit_extender_1_out, bit_extender_2_out,
       bit_extender_3_out, d, multiplier_1_out, negQ, not_1_out, sub1, sub1_d, sub1_s, subtractor_1_out;

  and and_1 (and_1_out, A_all[15], D_all[15]);
  Adder #(.width(16)) adder_1 (.a(16'h1), .b(not_1_out), .out(negQ));  // open: cin, cout
  assign not_1_out = ~Q;  // NOT_Gate not_1, 16 bits wide
  assign bit_extender_1_out = {{15{and_1_out}}, and_1_out};  // Bit_Extender bit_extender_1
  absVal absval_1 (.inp(A_all), .abso(a));
  absVal absval_2 (.inp(D_all), .abso(d));
  xor xor_1 (xor_1_out, A_all[15], D_all[15]);
  assign bit_extender_2_out = {{15{xor_1_out}}, xor_1_out};  // Bit_Extender bit_extender_2
  and and_2 (and_2_out, ~A_all[15], ~D_all[15]);  // AND_Gate
  assign bit_extender_3_out = {{15{and_2_out}}, and_2_out};  // Bit_Extender bit_extender_3
  assign sub1_s = sub1 & bit_extender_1_out;  // AND_Gate and_3, 16 bits wide
  assign and_4_out = bit_extender_1_out & Q;  // AND_Gate and_4, 16 bits wide
  Multiplier #(.width(16)) multiplier_1 (.a(Q), .b(d), .out(multiplier_1_out));  // open: cin, cout
  assign sub1_d = sub1 & bit_extender_2_out;  // AND_Gate and_5, 16 bits wide
  assign and_6_out = bit_extender_2_out & negQ;  // AND_Gate and_6, 16 bits wide
  assign and_7_out = bit_extender_3_out & Q;  // AND_Gate and_7, 16 bits wide
  Adder #(.width(16)) adder_2 (.a(and_4_out), .b(sub1_s), .out(adder_2_out));  // open: cin, cout
  Comparator #(.width(16)) comparator_1 (.a(multiplier_1_out), .b(a), .eq(comparator_1_eq));  // open: gt, lt
  Subtractor #(.width(16)) subtractor_1 (.a(and_6_out), .b(sub1_d), .out(subtractor_1_out));  // open: bin, bout
  not not_2 (not_2_out, comparator_1_eq);
  assign out_4 = subtractor_1_out | and_7_out | adder_2_out;  // OR_Gate or_1, 16 bits wide
  assign sub1 = {{15{1'b0}}, not_2_out};  // Bit_Extender bit_extender_4

  // Other names for the same wires on the sheet: a15 = A_all[15]; d15 = D_all[15]
endmodule

module absVal (
  input  [15:0] inp,
  output [15:0] abso
);

  wire [15:0] adder_1_out, and_1_out, and_2_out, bit_extender_1_out, not_1_out, not_2_out;

  assign not_1_out = ~inp;  // NOT_Gate not_1, 16 bits wide
  Adder #(.width(16)) adder_1 (.a(16'h1), .b(not_1_out), .out(adder_1_out));  // open: cin, cout
  assign bit_extender_1_out = {{15{inp[15]}}, inp[15]};  // Bit_Extender bit_extender_1
  assign and_1_out = adder_1_out & bit_extender_1_out;  // AND_Gate and_1, 16 bits wide
  assign not_2_out = ~bit_extender_1_out;  // NOT_Gate not_2, 16 bits wide
  assign and_2_out = not_2_out & inp;  // AND_Gate and_2, 16 bits wide
  assign abso = and_1_out | and_2_out;  // OR_Gate or_1, 16 bits wide
endmodule

module test2 (
  input  rst,
  input  req,
  input  [15:0] A,
  input  [15:0] D,
  output ack,
  output fdbz,
  output [15:0] out_7,
  output [15:0] out_8
);

  wire clock_1_out;

  Clock clock_1 (.out(clock_1_out));
  main main_1 (.CLK(clock_1_out), .RST(rst), .REQ(req), .A(A), .D(D), .ACK(ack), .FDBZ(fdbz), .Q(out_7), .R(out_8));
endmodule

module Divide (
  input  [15:0] Divident,
  input  [15:0] Divisor,
  input  REQ,
  input  RST,
  input  CLK,
  output [15:0] out_6
);

  wire clk_t, counter_1_carry, ld, nreq, subtractor_1_bout;
  wire [15:0] a_d, adder_1_out, adder_3_out, bit_extender_3_out, cur_a, cur_q, multiplexer_1_out,
       multiplexer_2_out, new_a, new_q, register_1_q, register_2_q;
  wire [31:0] adder_2_out, bit_extender_1_out, bit_extender_2_out, shifter_1_out;

  Clock clock_1 (.out(clk_t));
  Multiplexer #(.width(16), .enable("false")) multiplexer_1 (
    .in0(new_a), .in1({16{1'b0}}), .out(multiplexer_1_out), .sel(ld));
  Multiplexer #(.width(16), .enable("false")) multiplexer_2 (
    .in0(new_q), .in1(Divident), .out(multiplexer_2_out), .sel(ld));
  Register #(.width(16)) register_1 (.D(multiplexer_1_out), .clk(clk_t), .Q(register_1_q));  // open: en, clr
  Register #(.width(16)) register_2 (.D(multiplexer_2_out), .clk(clk_t), .Q(register_2_q));  // open: en, clr
  Subtractor #(.width(16)) subtractor_1 (.a(cur_a), .b(Divisor), .out(a_d), .bout(subtractor_1_bout));  // open: bin
  Adder #(.width(16)) adder_1 (.a(a_d), .b(Divisor), .out(adder_1_out));  // open: cin, cout
  not not_1 (nreq, REQ);
  load load_1 (.REQ(REQ), .RST(RST), .CLK(clk_t), .load(ld));
  assign bit_extender_1_out = {{16{register_1_q[15]}}, register_1_q};  // Bit_Extender bit_extender_1
  assign bit_extender_2_out = {{16{register_2_q[15]}}, register_2_q};  // Bit_Extender bit_extender_2
  Multiplexer #(.width(16), .enable("false")) multiplexer_3 (
    .in0(a_d), .in1(adder_1_out), .out(new_a), .sel(subtractor_1_bout));
  Shifter #(.width(32)) shifter_1 (.in(bit_extender_1_out), .\dist (5'b10000), .out(shifter_1_out));
  Adder #(.width(32)) adder_2 (.a(shifter_1_out), .b(bit_extender_2_out), .out(adder_2_out));  // open: cin, cout
  Counter #(.width(5), .max('h11), .ongoal("stay")) counter_1 (
    .clr(nreq), .clk(clk_t), .carry(counter_1_carry));  // open: load, up, count, D, Q
  Shifter #(.width(32)) shifter_2 (.in(adder_2_out), .\dist (5'b00001), .out({cur_a, cur_q}));
  Adder #(.width(16)) adder_3 (.a(cur_q), .b(16'h1), .out(adder_3_out));  // open: cin, cout
  // Probe on new_q
  Multiplexer #(.width(16), .enable("false")) multiplexer_4 (
    .in0(adder_3_out), .in1(cur_q), .out(new_q), .sel(subtractor_1_bout));
  assign out_6 = new_q & bit_extender_3_out;  // AND_Gate and_1, 16 bits wide
  assign bit_extender_3_out = {{15{counter_1_carry}}, counter_1_carry};  // Bit_Extender bit_extender_3

  // Other names for the same wires on the sheet: D[15:0] = Divisor
endmodule

module load (
  input  REQ,
  input  RST,
  input  CLK,
  output load
);

  wire and_1_out, and_2_out, d_ff_2_q, not_1_out, not_2_out, or_1_out;

  not not_1 (not_1_out, RST);
  and and_1 (and_1_out, not_2_out, REQ, ~d_ff_2_q, not_1_out);  // AND_Gate
  or or_1 (or_1_out, d_ff_2_q, load);
  not not_2 (not_2_out, load);
  D_Flip_Flop d_ff_1 (.D(and_1_out), .clk(CLK), .Q(load));  // open: Qn, preset, reset
  D_Flip_Flop d_ff_2 (.D(and_2_out), .clk(CLK), .Q(d_ff_2_q));  // open: Qn, preset, reset
  and and_2 (and_2_out, or_1_out, not_1_out, REQ);
endmodule

module test3 (
  input  [3:0] in_1,
  input  [3:0] in_2,
  input  in_3,
  input  in_4,
  input  in_5,
  output [3:0] out_6
);

  wire comparator_1_eq, counter_1_carry, ld, not_2_out, nreq, subtractor_1_bout;
  wire [2:0] multiplexer_3_out, subtractor_2_out;
  wire [3:0] a_d, adder_1_out, adder_3_out, bit_extender_3_out, cur_a, cur_q, multiplexer_1_out,
       multiplexer_2_out, new_a, new_q, register_1_q, register_2_q;
  wire [7:0] adder_2_out, bit_extender_1_out, bit_extender_2_out, shifter_1_out;

  not not_1 (nreq, in_3);
  Multiplexer #(.width(4), .enable("false")) multiplexer_1 (
    .in0(new_a), .in1(4'b0000), .out(multiplexer_1_out), .sel(ld));
  Multiplexer #(.width(4), .enable("false")) multiplexer_2 (.in0(new_q), .in1(in_1), .out(multiplexer_2_out), .sel(ld));
  Multiplexer #(.width(3), .enable("false")) multiplexer_3 (
    .in1(3'b101), .out(multiplexer_3_out), .sel(ld));  // open: in0
  Register #(.width(4)) register_1 (.D(multiplexer_1_out), .clk(in_5), .Q(register_1_q), .clr(nreq));  // open: en
  Register #(.width(4)) register_2 (.D(multiplexer_2_out), .clk(in_5), .Q(register_2_q), .clr(nreq));  // open: en
  Subtractor #(.width(4)) subtractor_1 (.a(cur_a), .b(in_2), .out(a_d), .bout(subtractor_1_bout));  // open: bin
  Adder #(.width(4)) adder_1 (.a(a_d), .b(in_2), .out(adder_1_out));  // open: cin, cout
  load load_1 (.REQ(in_3), .RST(in_4), .CLK(in_5), .load(ld));
  assign bit_extender_1_out = {{4{register_1_q[3]}}, register_1_q};  // Bit_Extender bit_extender_1
  assign bit_extender_2_out = {{4{1'b0}}, register_2_q};  // Bit_Extender bit_extender_2
  Multiplexer #(.width(4), .enable("false")) multiplexer_4 (
    .in0(a_d), .in1(adder_1_out), .out(new_a), .sel(subtractor_1_bout));
  Subtractor #(.width(3)) subtractor_2 (.a(multiplexer_3_out), .b(3'b001), .out(subtractor_2_out));  // open: bin, bout
  Shifter shifter_1 (.in(bit_extender_1_out), .\dist (3'b100), .out(shifter_1_out));
  Comparator #(.width(3)) comparator_1 (.a(subtractor_2_out), .b(3'b000), .eq(comparator_1_eq));  // open: gt, lt
  Adder adder_2 (.a(shifter_1_out), .b(bit_extender_2_out), .out(adder_2_out));  // open: cin, cout
  not not_2 (not_2_out, comparator_1_eq);
  Counter #(.width(3), .max('h5), .ongoal("stay")) counter_1 (
    .clr(nreq), .clk(in_5), .carry(counter_1_carry));  // open: load, up, count, D, Q
  Adder #(.width(4)) adder_3 (.a(cur_q), .b(4'b0001), .out(adder_3_out));  // open: cin, cout
  Shifter shifter_2 (.in(adder_2_out), .\dist (3'b001), .out({cur_a, cur_q}));
  // Probe on new_q
  Multiplexer #(.width(4), .enable("false")) multiplexer_5 (
    .in0(adder_3_out), .in1(cur_q), .out(new_q), .sel(subtractor_1_bout));
  assign bit_extender_3_out = {{3{counter_1_carry}}, counter_1_carry};  // Bit_Extender bit_extender_3
  assign out_6 = new_q & bit_extender_3_out;  // AND_Gate and_1, 4 bits wide

  // Other names for the same wires on the sheet: clk = in_5; D[3:0] = in_2; divident[3:0] = in_1
endmodule

module test4 (
  input  [15:0] A,
  input  [15:0] D,
  input  req,
  input  rst,
  input  clk,
  output [15:0] out_6,
  output ack
);

  wire comparator_1_eq, fi, ld, nreq, register_3_q, subtractor_1_bout, ufi;
  wire [4:0] counter_1_q;
  wire [15:0] a_d, adder_1_out, adder_3_out, bit_extender_3_out, cur_a, cur_q, multiplexer_1_out,
       multiplexer_2_out, new_a, new_q, register_1_q, register_2_q;
  wire [31:0] adder_2_out, bit_extender_1_out, bit_extender_2_out, shifter_1_out;

  not not_1 (nreq, req);
  Multiplexer #(.width(16), .enable("false")) multiplexer_1 (
    .in0(new_a), .in1({16{1'b0}}), .out(multiplexer_1_out), .sel(ld));
  Multiplexer #(.width(16), .enable("false")) multiplexer_2 (.in0(new_q), .in1(A), .out(multiplexer_2_out), .sel(ld));
  Register #(.width(16)) register_1 (.D(multiplexer_1_out), .en(ufi), .clk(clk), .Q(register_1_q), .clr(nreq));
  Register #(.width(16)) register_2 (.D(multiplexer_2_out), .en(ufi), .clk(clk), .Q(register_2_q), .clr(nreq));
  Subtractor #(.width(16)) subtractor_1 (.a(cur_a), .b(D), .out(a_d), .bout(subtractor_1_bout));  // open: bin
  Adder #(.width(16)) adder_1 (.a(a_d), .b(D), .out(adder_1_out));  // open: cin, cout
  load load_1 (.REQ(req), .RST(rst), .CLK(clk), .load(ld));
  assign bit_extender_1_out = {{16{register_1_q[15]}}, register_1_q};  // Bit_Extender bit_extender_1
  assign bit_extender_2_out = {{16{1'b0}}, register_2_q};  // Bit_Extender bit_extender_2
  Multiplexer #(.width(16), .enable("false")) multiplexer_3 (
    .in0(a_d), .in1(adder_1_out), .out(new_a), .sel(subtractor_1_bout));
  Shifter #(.width(32)) shifter_1 (.in(bit_extender_1_out), .\dist (5'b10000), .out(shifter_1_out));
  Counter #(.width(5), .max('h11), .ongoal("stay")) counter_1 (
    .clr(nreq), .clk(clk), .carry(fi), .Q(counter_1_q));  // open: load, up, count, D
  Adder #(.width(32)) adder_2 (.a(shifter_1_out), .b(bit_extender_2_out), .out(adder_2_out));  // open: cin, cout
  Adder #(.width(16)) adder_3 (.a(cur_q), .b(16'h1), .out(adder_3_out));  // open: cin, cout
  Shifter #(.width(32)) shifter_2 (.in(adder_2_out), .\dist (5'b00001), .out({cur_a, cur_q}));
  // Probe on new_q
  Multiplexer #(.width(16), .enable("false")) multiplexer_4 (
    .in0(adder_3_out), .in1(cur_q), .out(new_q), .sel(subtractor_1_bout));
  not not_2 (ufi, fi);
  Comparator #(.width(5)) comparator_1 (.a(5'b10001), .b(counter_1_q), .eq(comparator_1_eq));  // open: gt, lt
  assign bit_extender_3_out = {{15{comparator_1_eq}}, comparator_1_eq};  // Bit_Extender bit_extender_3
  assign out_6 = new_q & bit_extender_3_out;  // AND_Gate and_1, 16 bits wide
  Register #(.width(1)) register_3 (.D(fi), .clk(clk), .Q(register_3_q));  // open: en, clr
  and and_2 (ack, register_3_q, ~rst);  // AND_Gate

  // Other names for the same wires on the sheet: divident[15:0] = A
endmodule
