// Logisim project final.circ as structural Verilog: 7 circuits, main circuit FSM_2PHS
module FSM_2PHS (
  input  CLK,
  input  RST,
  input  REQ,
  input  DONE,
  output ACK,
  output GO
);

  wire and_1_out, and_2_out, and_3_out, and_4_out, and_5_out, and_6_out, and_7_out, and_8_out, next0, next1,
       next2, next3, not_1_out, or_1_out, or_2_out, or_3_out, s0, s1, s2, s3;

  D_Flip_Flop d_ff_1 (.D(next0), .clk(CLK), .Q(s0));  // open: Qn, preset, reset
  D_Flip_Flop d_ff_2 (.D(next1), .clk(CLK), .Q(s1));  // open: Qn, preset, reset
  D_Flip_Flop d_ff_3 (.D(next2), .clk(CLK), .Q(s2));  // open: Qn, preset, reset
  D_Flip_Flop d_ff_4 (.D(next3), .clk(CLK), .Q(s3));  // open: Qn, preset, reset
  not not_1 (not_1_out, REQ);
  and and_1 (and_1_out, not_1_out, s0);
  and and_2 (and_2_out, DONE, s3);
  and and_3 (and_3_out, REQ, s0);
  and and_4 (and_4_out, ~DONE, s1);  // AND_Gate
  and and_5 (and_5_out, DONE, s1);
  and and_6 (and_6_out, REQ, s2);
  and and_7 (and_7_out, ~DONE, s3);  // AND_Gate
  and and_8 (and_8_out, ~REQ, s2);  // AND_Gate
  or or_1 (or_1_out, and_3_out, and_4_out);
  or or_2 (or_2_out, and_5_out, and_6_out);
  or or_3 (or_3_out, and_7_out, and_8_out);
  or or_4 (next0, RST, and_1_out, and_2_out);
  and and_9 (next1, ~RST, or_1_out);  // AND_Gate
  and and_10 (next2, ~RST, or_2_out);  // AND_Gate
  and and_11 (next3, ~RST, or_3_out);  // AND_Gate
  or or_5 (ACK, s2, s3);
  or or_6 (GO, s1, s3);

  // Notes on the sheet:
  //   You Need to Edit This
  //   Two Phase Handshake FSM from Part 1
  //   Do not move/delete/add/rename pins
endmodule

module TB_FSM_2PHS (
  input  REQ,
  input  [31:0] X,
  output [31:0] out_3,
  output [31:0] X_SQUARE
);

  wire CLK_out, DUT_ack, DUT_go, poweron_reset_random_1_rst, rnddlymul_1_done;

  Clock sysclk ();  // open: out
  Clock CLK (.out(CLK_out));
  poweron_reset_random poweron_reset_random_1 (.CLK(CLK_out), .RST(poweron_reset_random_1_rst));
  LED REQis1 (.in(poweron_reset_random_1_rst));
  LED ACKis1 (.in(DUT_ack));
  FSM_2PHS DUT (
    .CLK(CLK_out), .RST(poweron_reset_random_1_rst), .REQ(REQ), .DONE(rnddlymul_1_done), .ACK(DUT_ack),
    .GO(DUT_go));
  RndDlyMul rnddlymul_1 (
    .CLK(CLK_out), .GO(DUT_go), .A(X), .B(X), .DONE(rnddlymul_1_done), .AxBLo(X_SQUARE), .AxBHi(out_3));

  // Notes on the sheet:
  //   Simple testbench for manual testing of FSM_2PHS
  //   Feel free to edit it for your needs.
endmodule

module FSM_SQROOT (
  input  CLK,
  input  RST,
  input  GO,
  input  STATUS,
  output DONE,
  output COMMAND
);


  assign COMMAND = GO;
  assign DONE = STATUS;

  // Notes on the sheet:
  //   You Need to Edit This
  //   Controller for Part 2
  //   Modify Status and Command signals for Datapath
  //   If you don't need controller, just feed GO to COMMAND, and STATUS to DONE
endmodule

module DP_SQROOT (
  input  CLK,
  input  RST,
  input  COMMAND,
  input  [15:0] DIN,
  output STATUS,
  output [7:0] DOUT
);

  wire and_1_out, and_2_out, and_6_out, better, bigger, comparator_3_gt, counter_1_carry, eq, ld, or_1_out,
       or_3_out, or_4_out, smaller;
  wire [7:0] bit_extender_4_out, counter_1_q;
  wire [15:0] adder_1_out, and_3_out, and_4_out, and_5_out, b_i, bit_extender_1_out, bit_extender_2_out,
       bit_extender_3_out, cur_diff, diff, i, i2, multiplexer_1_out, multiplexer_5_out, n_diff, n_i,
       shifter_1_out, shifter_2_out, subtractor_2_out, subtractor_3_out;

  Multiplexer #(.width(16), .enable("false")) multiplexer_1 (
    .in0(n_i), .in1({16{1'b0}}), .out(multiplexer_1_out), .sel(ld));
  or or_1 (or_1_out, eq, ~better);  // OR_Gate
  Register #(.width(16)) register_1 (.D(multiplexer_1_out), .clk(CLK), .Q(i));  // open: en, clr
  assign bit_extender_1_out = {{15{or_1_out}}, or_1_out};  // Bit_Extender bit_extender_1
  and and_1 (and_1_out, better, bigger);
  Shifter #(.width(16), .shift("ar")) shifter_1 (.in(i), .\dist (4'b0001), .out(shifter_1_out));
  and and_2 (and_2_out, better, smaller);
  Adder #(.width(16)) adder_1 (.a(i), .b(16'hfe), .out(adder_1_out));  // open: cin, cout
  load load_1 (.go(COMMAND), .CLK(CLK), .load(ld));
  assign and_3_out = bit_extender_1_out & i;  // AND_Gate and_3, 16 bits wide
  assign bit_extender_2_out = {{15{and_1_out}}, and_1_out};  // Bit_Extender bit_extender_2
  assign bit_extender_3_out = {{15{and_2_out}}, and_2_out};  // Bit_Extender bit_extender_3
  Shifter #(.width(16), .shift("ar")) shifter_2 (.in(adder_1_out), .\dist (4'b0001), .out(shifter_2_out));
  Multiplexer #(.width(16), .enable("false")) multiplexer_2 (.in0(and_3_out), .in1(b_i), .out(n_i), .sel(better));
  assign and_4_out = bit_extender_2_out & shifter_1_out;  // AND_Gate and_4, 16 bits wide
  assign and_5_out = bit_extender_3_out & shifter_2_out;  // AND_Gate and_5, 16 bits wide
  Bit_Extender #(.in_width(16), .out_width(8)) bit_extender_4 (.in(i), .out(bit_extender_4_out));
  Multiplier #(.width(16)) multiplier_1 (.a(i), .b(i), .out(i2));  // open: cin, cout
  Comparator #(.width(16), .mode("unsigned")) comparator_1 (.a(i2), .b(DIN), .gt(bigger), .eq(eq), .lt(smaller));
  // OR_Gate or_2 has open pins: in0=and_4_out, in1=and_5_out, out=open
  Subtractor subtractor_1 (.a(bit_extender_4_out), .b(8'h1), .out(DOUT));  // open: bin, bout
  Subtractor #(.width(16)) subtractor_2 (.a(DIN), .b(i2), .out(subtractor_2_out));  // open: bin, bout
  Subtractor #(.width(16)) subtractor_3 (.a(i2), .b(DIN), .out(subtractor_3_out));  // open: bin, bout
  Adder #(.width(16)) adder_2 (.a(i), .b(16'h1), .out(b_i));  // open: cin, cout
  Multiplexer #(.width(16), .enable("false")) multiplexer_3 (
    .in0(subtractor_2_out), .in1(subtractor_3_out), .out(cur_diff), .sel(bigger));
  Multiplexer #(.width(16), .enable("false")) multiplexer_4 (.in0(diff), .in1(cur_diff), .out(n_diff), .sel(better));
  Register #(.width(16)) register_2 (.D(multiplexer_5_out), .clk(CLK), .Q(diff));  // open: en, clr
  Multiplexer #(.width(16), .enable("false")) multiplexer_5 (
    .in0(n_diff), .in1({16{1'b1}}), .out(multiplexer_5_out), .sel(ld));
  Comparator #(.width(16), .mode("unsigned")) comparator_2 (.a(cur_diff), .b(diff), .lt(better));  // open: gt, eq
  Counter #(.ongoal("stay")) counter_1 (
    .clr(or_3_out), .clk(CLK), .carry(counter_1_carry), .Q(counter_1_q));  // open: load, up, count, D
  or or_3 (or_3_out, ~COMMAND, RST);  // OR_Gate
  or or_4 (or_4_out, counter_1_carry, ~better);  // OR_Gate
  and and_6 (and_6_out, or_4_out, ~RST, COMMAND);  // AND_Gate
  Comparator #(.mode("unsigned")) comparator_3 (.a(counter_1_q), .b(8'h1), .gt(comparator_3_gt));  // open: eq, lt
  and and_7 (STATUS, and_6_out, comparator_3_gt);

  // Other names for the same wires on the sheet: done = STATUS; go = COMMAND

  // Notes on the sheet:
  //   You Need to Edit This
  //   Datapath for Part 2
  //   Modify Status and Command signals for Controller
  //   If you don't have a controller then COMMAND is GO, and STATUS is DONE
endmodule

module MAIN (
  input  CLK,
  input  RST,
  input  REQ,
  input  [15:0] DIN,
  output ACK,
  output [7:0] DOUT
);

  wire dp_sqroot_1_status, fsm_2phs_1_go, fsm_sqroot_1_command, fsm_sqroot_1_done;

  FSM_2PHS fsm_2phs_1 (.CLK(CLK), .RST(RST), .REQ(REQ), .DONE(fsm_sqroot_1_done), .ACK(ACK), .GO(fsm_2phs_1_go));
  FSM_SQROOT fsm_sqroot_1 (
    .CLK(CLK), .RST(RST), .GO(fsm_2phs_1_go), .STATUS(dp_sqroot_1_status), .DONE(fsm_sqroot_1_done),
    .COMMAND(fsm_sqroot_1_command));
  DP_SQROOT dp_sqroot_1 (
    .CLK(CLK), .RST(RST), .COMMAND(fsm_sqroot_1_command), .DIN(DIN), .STATUS(dp_sqroot_1_status), .DOUT(DOUT));

  // Notes on the sheet:
  //   No Need to Edit This
endmodule

module TB_MAIN (
  input  REQ,
  input  [15:0] DIN,
  output [7:0] DOUT
);

  wire CLK_out, DUT_ack, poweron_reset_random_1_rst;

  Clock sysclk ();  // open: out
  Clock CLK (.out(CLK_out));
  poweron_reset_random poweron_reset_random_1 (.CLK(CLK_out), .RST(poweron_reset_random_1_rst));
  LED REQis1 (.in(poweron_reset_random_1_rst));
  LED ACKis1 (.in(DUT_ack));
  MAIN DUT (.CLK(CLK_out), .RST(poweron_reset_random_1_rst), .REQ(REQ), .DIN(DIN), .ACK(DUT_ack), .DOUT(DOUT));

  // Notes on the sheet:
  //   X
  //   Testbench for manual testing of MAIN system
  //   Feel free to edit it for your needs.
  //   sqrt(X)
endmodule

module load (
  input  go,
  input  CLK,
  output load
);

  wire and_2_out, and_3_out, next0, next1, next2, s0, s2;

  D_Flip_Flop d_ff_1 (.D(next0), .clk(CLK), .Q(s0));  // open: Qn, preset, reset
  D_Flip_Flop d_ff_2 (.D(next1), .clk(CLK), .Q(load));  // open: Qn, preset, reset
  D_Flip_Flop d_ff_3 (.D(next2), .clk(CLK), .Q(s2));  // open: Qn, preset, reset
  not not_1 (next0, go);
  and and_1 (next1, s0, go);
  and and_2 (and_2_out, load, go);
  and and_3 (and_3_out, s2, go);
  or or_1 (next2, and_2_out, and_3_out);

  // Other names for the same wires on the sheet: din = go; s1 = load
endmodule
